// Logisim project Gaev_Efimov_Masolygin_24216_Checkers_Logisim.circ as structural Verilog: 20 circuits, main circuit main
module main (
);

  wire _1_2_out, _1_out, _2_2_out, _2_out, _2k1_bin, _2k_bin, _3_2_out, _3_out, _4_2_out, _4_out, _5_2_out,
       _5_out, _6_2_out, _6_out, _7_2_out, _7_out, _8_2_out, _8_out, A_2_out, A_out, and_1_out, and_2_out,
       and_3_out, and_4_out, B_2_out, B_out, buffer_1_out, buffer_2_out, buffer_3_out, button_1_out,
       button_confirm, C_2_out, C_out, cdm_processing_1_code2_5, clear_button, clock, code_reset,
       controlled_buffer_1_out, controlled_buffer_2_out, counter_2_carry, D_2_out, D_out,
       demultiplexer_1_out0, demultiplexer_1_out1, demultiplexer_1_out2, demultiplexer_1_out3,
       demultiplexer_1_out4, demultiplexer_1_out5, demultiplexer_1_out6, demultiplexer_1_out7, E_2_out,
       E_out, editing, editing_cdm, enter, F_2_out, F_out, G_2_out, G_out, H_2_out, H_out, \is_сapture ,
       lock, map_1_out_13, not_2_out, or_6_out, possibly_move, reset, stop_editing;
  wire [1:0] counter, counter_cdm, or_1_out;
  wire [2:0] bit_extender_1_out;
  wire [3:0] bot_lvl, button_decoder_1_output_digit, button_decoder_1_output_digit_2,
       button_decoder_2_output_digit, button_decoder_2_output_digit_2, code, coord_0_input, coord_1_input,
       coord_2_input, coord_3_input, coord_4_input, coord_5_input, coord_6_input, coord_7_input;
  wire [4:0] draw_board_1_out_17_2, draw_board_1_out_17_3, draw_board_1_out_17_4, draw_board_1_out_18_2,
       draw_board_1_out_18_3, draw_board_1_out_18_4, draw_board_1_out_19_2, draw_board_1_out_19_3,
       draw_board_1_out_19_4, draw_board_1_out_20_2, draw_board_1_out_20_3, draw_board_1_out_20_4,
       draw_board_1_out_21_2, draw_board_1_out_21_3, draw_board_1_out_21_4, draw_board_1_out_22_2,
       draw_board_1_out_22_3, draw_board_1_out_22_4, draw_board_1_out_23_2, draw_board_1_out_23_3,
       draw_board_1_out_23_4, draw_board_1_out_24_2, draw_board_1_out_24_3, draw_board_1_out_25_2,
       draw_board_1_out_25_3, draw_board_1_out_25_4, draw_board_1_out_26_2, draw_board_1_out_26_3,
       draw_board_1_out_26_4, draw_board_1_out_27_2, draw_board_1_out_27_3, draw_board_1_out_27_4,
       draw_board_1_out_28_2, draw_board_1_out_28_3, draw_board_1_out_28_4, draw_board_1_out_29_2,
       draw_board_1_out_29_3, draw_board_1_out_29_4, draw_board_1_out_30_2, draw_board_1_out_30_3,
       draw_board_1_out_30_4, draw_board_1_out_31_2, draw_board_1_out_31_3, draw_board_1_out_31_4,
       draw_board_1_out_32_2, draw_board_1_out_32_3, draw_board_1_out_33_2, draw_board_1_out_33_3,
       draw_board_1_out_33_4, draw_board_1_out_34_2, draw_board_1_out_34_3, draw_board_1_out_34_4,
       draw_board_1_out_35_2, draw_board_1_out_35_3, draw_board_1_out_35_4, draw_board_1_out_36_2,
       draw_board_1_out_36_3, draw_board_1_out_36_4, draw_board_1_out_37_2, draw_board_1_out_37_3,
       draw_board_1_out_37_4, draw_board_1_out_38_2, draw_board_1_out_38_3, draw_board_1_out_38_4,
       draw_board_1_out_39_2, draw_board_1_out_39_3, draw_board_1_out_39_4, draw_board_1_out_40_2,
       draw_board_1_out_40_3, draw_board_1_out_41_2, draw_board_1_out_41_3, draw_board_1_out_41_4,
       draw_board_1_out_42_2, draw_board_1_out_42_3, draw_board_1_out_42_4, draw_board_1_out_43_2,
       draw_board_1_out_43_3, draw_board_1_out_43_4, draw_board_1_out_44_2, draw_board_1_out_44_3,
       draw_board_1_out_44_4, draw_board_1_out_45_2, draw_board_1_out_45_3, draw_board_1_out_45_4,
       draw_board_1_out_46_2, draw_board_1_out_46_3, draw_board_1_out_46_4, draw_board_1_out_47_2,
       draw_board_1_out_47_3, draw_board_1_out_47_4, draw_board_1_out_48_2, draw_board_1_out_48_3,
       draw_board_1_out_49_2, draw_board_1_out_49_3, draw_board_1_out_49_4, draw_board_1_out_50_2,
       draw_board_1_out_50_3, draw_board_1_out_50_4, draw_board_1_out_51_2, draw_board_1_out_51_3,
       draw_board_1_out_51_4, draw_board_1_out_52_2, draw_board_1_out_52_3, draw_board_1_out_52_4,
       draw_board_1_out_53_2, draw_board_1_out_53_3, draw_board_1_out_53_4, draw_board_1_out_54_2,
       draw_board_1_out_54_3, draw_board_1_out_54_4, draw_board_1_out_55_2, draw_board_1_out_55_3,
       draw_board_1_out_55_4, draw_board_1_out_56_2, draw_board_1_out_56_3, draw_board_1_out_57_2,
       draw_board_1_out_57_3, draw_board_1_out_57_4, draw_board_1_out_58_2, draw_board_1_out_58_3,
       draw_board_1_out_58_4, draw_board_1_out_59_2, draw_board_1_out_59_3, draw_board_1_out_59_4,
       draw_board_1_out_60_2, draw_board_1_out_60_3, draw_board_1_out_60_4, draw_board_1_out_61_2,
       draw_board_1_out_61_3, draw_board_1_out_61_4, draw_board_1_out_62_2, draw_board_1_out_62_3,
       draw_board_1_out_62_4, draw_board_1_out_63_2, draw_board_1_out_63_3, draw_board_1_out_63_4,
       draw_board_1_out_64_2, draw_board_1_out_64_3, draw_board_1_out_65_2, draw_board_1_out_65_3,
       draw_board_1_out_65_4, draw_board_1_out_66_2, draw_board_1_out_66_3, draw_board_1_out_66_4,
       draw_board_1_out_67_2, draw_board_1_out_67_3, draw_board_1_out_67_4, draw_board_1_out_68_2,
       draw_board_1_out_68_3, draw_board_1_out_68_4, draw_board_1_out_69_2, draw_board_1_out_69_3,
       draw_board_1_out_69_4, draw_board_1_out_70_2, draw_board_1_out_70_3, draw_board_1_out_70_4,
       draw_board_1_out_71_2, draw_board_1_out_71_3, draw_board_1_out_71_4, draw_board_1_out_72_2,
       draw_board_1_out_72_3, draw_board_1_out_73_2, draw_board_1_out_73_3, draw_board_1_out_73_4,
       draw_board_1_out_74_2, draw_board_1_out_74_3, draw_board_1_out_74_4, draw_board_1_out_75_2,
       draw_board_1_out_75_3, draw_board_1_out_75_4, draw_board_1_out_76_2, draw_board_1_out_76_3,
       draw_board_1_out_76_4, draw_board_1_out_77_2, draw_board_1_out_77_3, draw_board_1_out_77_4,
       draw_board_1_out_78_2, draw_board_1_out_78_3, draw_board_1_out_78_4, draw_board_1_out_79_2,
       draw_board_1_out_79_3, draw_board_1_out_79_4, draw_board_1_out_80_2, draw_board_1_out_80_3;
  wire [7:0] between_digit, between_digit_cdm, button_decoder_1_output_letter,
       button_decoder_2_output_letter, from_digit, from_digit_cdm, from_letter, from_letter_t, or_5_out,
       or_7_out, or_8_out, to_digit, to_digit_cdm, to_letter, to_letter_t;
  wire [7:1] map_1_out_11;
  wire [9:0] draw_board_1_out_17, draw_board_1_out_18, draw_board_1_out_19, draw_board_1_out_20,
       draw_board_1_out_21, draw_board_1_out_22, draw_board_1_out_23, draw_board_1_out_25,
       draw_board_1_out_26, draw_board_1_out_27, draw_board_1_out_28, draw_board_1_out_29,
       draw_board_1_out_30, draw_board_1_out_31, draw_board_1_out_33, draw_board_1_out_34,
       draw_board_1_out_35, draw_board_1_out_36, draw_board_1_out_37, draw_board_1_out_38,
       draw_board_1_out_39, draw_board_1_out_41, draw_board_1_out_42, draw_board_1_out_43,
       draw_board_1_out_44, draw_board_1_out_45, draw_board_1_out_46, draw_board_1_out_47,
       draw_board_1_out_49, draw_board_1_out_50, draw_board_1_out_51, draw_board_1_out_52,
       draw_board_1_out_53, draw_board_1_out_54, draw_board_1_out_55, draw_board_1_out_57,
       draw_board_1_out_58, draw_board_1_out_59, draw_board_1_out_60, draw_board_1_out_61,
       draw_board_1_out_62, draw_board_1_out_63, draw_board_1_out_65, draw_board_1_out_66,
       draw_board_1_out_67, draw_board_1_out_68, draw_board_1_out_69, draw_board_1_out_70,
       draw_board_1_out_71, draw_board_1_out_73, draw_board_1_out_74, draw_board_1_out_75,
       draw_board_1_out_76, draw_board_1_out_77, draw_board_1_out_78, draw_board_1_out_79;
  wire [14:0] draw_board_1_out_24, draw_board_1_out_32, draw_board_1_out_40, draw_board_1_out_48,
       draw_board_1_out_56, draw_board_1_out_64, draw_board_1_out_72, draw_board_1_out_80;
  wire [15:0] ln1, ln2, ln3;
  wire [24:0] coord_0_output, coord_1_output, coord_2_output, coord_3_output, coord_4_output, coord_5_output,
       coord_6_output, coord_7_output;
  wire [31:0] between_line_output, between_line_output_cdm, between_line_output_hardware, displey_1__1,
       displey_1__2, displey_1__3, displey_1__4, displey_1__5, displey_1__6, displey_1__6_2,
       from_line_output, from_line_output_cdm, from_line_output_hardware, to_line_output, to_line_output_cdm,
       to_line_output_hardware;

  Clock clock_1 (.out(clock));
  buf buffer_1 (buffer_1_out, buffer_1_out);
  assign or_1_out = counter | counter_cdm;  // OR_Gate or_1, 2 bits wide
  assign from_line_output = from_line_output_cdm | from_line_output_hardware;  // OR_Gate or_2, 32 bits wide
  assign between_line_output = between_line_output_cdm | between_line_output_hardware;  // OR_Gate or_3, 32 bits wide
  assign to_line_output = to_line_output_cdm | to_line_output_hardware;  // OR_Gate or_4, 32 bits wide
  signa_extension signa_extension_1 (.enter(enter), .button(button_confirm), .clock(clock), .reset(reset));
  assign or_5_out = from_digit | from_digit_cdm;  // OR_Gate or_5, 8 bits wide
  or or_6 (or_6_out, editing, editing_cdm);
  parsing_data parsing_data_1 (.in_1(ln3), .out_3(to_line_output_cdm), .out_2(to_digit_cdm));
  parsing_data parsing_data_2 (.in_1(ln2), .out_3(between_line_output_cdm), .out_2(between_digit_cdm));
  parsing_data parsing_data_3 (.in_1(ln1), .out_3(from_line_output_cdm), .out_2(from_digit_cdm));
  assign or_7_out = between_digit | between_digit_cdm;  // OR_Gate or_7, 8 bits wide
  map map_1 (
    .out_11({map_1_out_11, _2k1_bin}), .clock(clock),
    .out_12({coord_7_input, coord_6_input, coord_5_input, coord_4_input, coord_3_input, coord_2_input, coord_1_input, coord_0_input}),
    .out_13(map_1_out_13), .from_index(or_5_out), .to_index(or_8_out), .between_index(or_7_out),
    .overwriting_input(from_line_output), .counter(or_1_out), .editing(or_6_out), .reset(reset),
    .overwriting_input_2(between_line_output), .overwriting_input_3(to_line_output));
  cdm_processing cdm_processing_1 (
    .from_digit(from_digit), .from_letter(from_letter_t), .to_digit(to_digit), .to_letter(to_letter_t),
    .out_9(editing_cdm), .counter(counter_cdm), .in_7(and_1_out), .in_1(clock), .out_16(code_reset),
    .out_12(ln3), .out_13(ln2), .out_14(ln1), .code2_5(cdm_processing_1_code2_5), .lock(lock), .code(code),
    .in_2(bot_lvl));
  and and_1 (and_1_out, enter, possibly_move, editing);
  assign or_8_out = to_digit_cdm | to_digit;  // OR_Gate or_8, 8 bits wide
  Bit_Extender #(.out_width(3), .\type ("sign")) bit_extender_1 (
    .in({map_1_out_11, _2k1_bin}), .out(bit_extender_1_out));
  not not_1 (_2k_bin, _2k1_bin);
  Hex_Digit_Display hex_digit_display_1 (.value(bot_lvl));  // open: dp
  lvl_bot lvl_bot_1 (.out_3(bot_lvl), .in_2(button_1_out), .in_1(button_confirm));
  Button button_1 (.out(button_1_out));
  buf buffer_2 (buffer_2_out, buffer_2_out);
  Counter #(.width(1), .max('h1)) counter_1 (
    .Q(\is_сapture ), .clk(cdm_processing_1_code2_5), .clr(and_2_out));  // open: load, D, count, carry
  and and_2 (and_2_out, reset, ~stop_editing);  // AND_Gate
  Demultiplexer #(.select(3), .enable("false")) demultiplexer_1 (
    .out0(demultiplexer_1_out0), .out1(demultiplexer_1_out1), .out2(demultiplexer_1_out2),
    .out3(demultiplexer_1_out3), .out4(demultiplexer_1_out4), .out5(demultiplexer_1_out5),
    .out6(demultiplexer_1_out6), .out7(demultiplexer_1_out7), .in(not_2_out), .sel(bit_extender_1_out));
  not not_2 (not_2_out, map_1_out_13);
  coord_convert coord_convert_1 (
    .in_9(_2k_bin), .in_10(_2k1_bin), .in_1(coord_0_input), .in_2(coord_1_input), .in_3(coord_2_input),
    .in_4(coord_3_input), .in_5(coord_4_input), .in_6(coord_5_input), .in_7(coord_6_input),
    .in_8(coord_7_input), .out_11(coord_0_output), .out_12(coord_1_output), .out_13(coord_2_output),
    .out_14(coord_3_output), .out_15(coord_4_output), .out_16(coord_5_output), .out_17(coord_6_output),
    .out_18(coord_7_output));
  DotMatrix #(.matrixrows(5)) dotmatrix_1 (
    .col0(draw_board_1_out_32_3), .col1(draw_board_1_out_32_2), .col2(draw_board_1_out_32[14:10]),
    .col3(draw_board_1_out_32[9:5]), .col4(draw_board_1_out_32[4:0]));
  DotMatrix #(.matrixrows(5)) dotmatrix_2 (
    .col0(draw_board_1_out_24_3), .col1(draw_board_1_out_24_2), .col2(draw_board_1_out_24[14:10]),
    .col3(draw_board_1_out_24[9:5]), .col4(draw_board_1_out_24[4:0]));
  DotMatrix #(.matrixrows(5)) dotmatrix_3 (
    .col0(draw_board_1_out_23_4), .col1(draw_board_1_out_23_3), .col2(draw_board_1_out_23_2),
    .col3(draw_board_1_out_23[9:5]), .col4(draw_board_1_out_23[4:0]));
  DotMatrix #(.matrixrows(5)) dotmatrix_4 (
    .col0(draw_board_1_out_31_4), .col1(draw_board_1_out_31_3), .col2(draw_board_1_out_31_2),
    .col3(draw_board_1_out_31[9:5]), .col4(draw_board_1_out_31[4:0]));
  DotMatrix #(.matrixrows(5)) dotmatrix_5 (
    .col0(draw_board_1_out_30_4), .col1(draw_board_1_out_30_3), .col2(draw_board_1_out_30_2),
    .col3(draw_board_1_out_30[9:5]), .col4(draw_board_1_out_30[4:0]));
  DotMatrix #(.matrixrows(5)) dotmatrix_6 (
    .col0(draw_board_1_out_22_4), .col1(draw_board_1_out_22_3), .col2(draw_board_1_out_22_2),
    .col3(draw_board_1_out_22[9:5]), .col4(draw_board_1_out_22[4:0]));
  DotMatrix #(.matrixrows(5)) dotmatrix_7 (
    .col0(draw_board_1_out_21_4), .col1(draw_board_1_out_21_3), .col2(draw_board_1_out_21_2),
    .col3(draw_board_1_out_21[9:5]), .col4(draw_board_1_out_21[4:0]));
  DotMatrix #(.matrixrows(5)) dotmatrix_8 (
    .col0(draw_board_1_out_29_4), .col1(draw_board_1_out_29_3), .col2(draw_board_1_out_29_2),
    .col3(draw_board_1_out_29[9:5]), .col4(draw_board_1_out_29[4:0]));
  DotMatrix #(.matrixrows(5)) dotmatrix_9 (
    .col0(draw_board_1_out_28_4), .col1(draw_board_1_out_28_3), .col2(draw_board_1_out_28_2),
    .col3(draw_board_1_out_28[9:5]), .col4(draw_board_1_out_28[4:0]));
  DotMatrix #(.matrixrows(5)) dotmatrix_10 (
    .col0(draw_board_1_out_20_4), .col1(draw_board_1_out_20_3), .col2(draw_board_1_out_20_2),
    .col3(draw_board_1_out_20[9:5]), .col4(draw_board_1_out_20[4:0]));
  DotMatrix #(.matrixrows(5)) dotmatrix_11 (
    .col0(draw_board_1_out_27_4), .col1(draw_board_1_out_27_3), .col2(draw_board_1_out_27_2),
    .col3(draw_board_1_out_27[9:5]), .col4(draw_board_1_out_27[4:0]));
  DotMatrix #(.matrixrows(5)) dotmatrix_12 (
    .col0(draw_board_1_out_19_4), .col1(draw_board_1_out_19_3), .col2(draw_board_1_out_19_2),
    .col3(draw_board_1_out_19[9:5]), .col4(draw_board_1_out_19[4:0]));
  DotMatrix #(.matrixrows(5)) dotmatrix_13 (
    .col0(draw_board_1_out_18_4), .col1(draw_board_1_out_18_3), .col2(draw_board_1_out_18_2),
    .col3(draw_board_1_out_18[9:5]), .col4(draw_board_1_out_18[4:0]));
  DotMatrix #(.matrixrows(5)) dotmatrix_14 (
    .col0(draw_board_1_out_26_4), .col1(draw_board_1_out_26_3), .col2(draw_board_1_out_26_2),
    .col3(draw_board_1_out_26[9:5]), .col4(draw_board_1_out_26[4:0]));
  DotMatrix #(.matrixrows(5)) dotmatrix_15 (
    .col0(draw_board_1_out_17_4), .col1(draw_board_1_out_17_3), .col2(draw_board_1_out_17_2),
    .col3(draw_board_1_out_17[9:5]), .col4(draw_board_1_out_17[4:0]));
  DotMatrix #(.matrixrows(5)) dotmatrix_16 (
    .col0(draw_board_1_out_25_4), .col1(draw_board_1_out_25_3), .col2(draw_board_1_out_25_2),
    .col3(draw_board_1_out_25[9:5]), .col4(draw_board_1_out_25[4:0]));
  DotMatrix #(.matrixrows(5)) dotmatrix_17 (
    .col0(draw_board_1_out_40_3), .col1(draw_board_1_out_40_2), .col2(draw_board_1_out_40[14:10]),
    .col3(draw_board_1_out_40[9:5]), .col4(draw_board_1_out_40[4:0]));
  DotMatrix #(.matrixrows(5)) dotmatrix_18 (
    .col0(draw_board_1_out_39_4), .col1(draw_board_1_out_39_3), .col2(draw_board_1_out_39_2),
    .col3(draw_board_1_out_39[9:5]), .col4(draw_board_1_out_39[4:0]));
  DotMatrix #(.matrixrows(5)) dotmatrix_19 (
    .col0(draw_board_1_out_38_4), .col1(draw_board_1_out_38_3), .col2(draw_board_1_out_38_2),
    .col3(draw_board_1_out_38[9:5]), .col4(draw_board_1_out_38[4:0]));
  DotMatrix #(.matrixrows(5)) dotmatrix_20 (
    .col0(draw_board_1_out_37_4), .col1(draw_board_1_out_37_3), .col2(draw_board_1_out_37_2),
    .col3(draw_board_1_out_37[9:5]), .col4(draw_board_1_out_37[4:0]));
  DotMatrix #(.matrixrows(5)) dotmatrix_21 (
    .col0(draw_board_1_out_36_4), .col1(draw_board_1_out_36_3), .col2(draw_board_1_out_36_2),
    .col3(draw_board_1_out_36[9:5]), .col4(draw_board_1_out_36[4:0]));
  DotMatrix #(.matrixrows(5)) dotmatrix_22 (
    .col0(draw_board_1_out_35_4), .col1(draw_board_1_out_35_3), .col2(draw_board_1_out_35_2),
    .col3(draw_board_1_out_35[9:5]), .col4(draw_board_1_out_35[4:0]));
  DotMatrix #(.matrixrows(5)) dotmatrix_23 (
    .col0(draw_board_1_out_34_4), .col1(draw_board_1_out_34_3), .col2(draw_board_1_out_34_2),
    .col3(draw_board_1_out_34[9:5]), .col4(draw_board_1_out_34[4:0]));
  DotMatrix #(.matrixrows(5)) dotmatrix_24 (
    .col0(draw_board_1_out_33_4), .col1(draw_board_1_out_33_3), .col2(draw_board_1_out_33_2),
    .col3(draw_board_1_out_33[9:5]), .col4(draw_board_1_out_33[4:0]));
  DotMatrix #(.inputtype("row"), .matrixcols(32)) dotmatrix_25 (
    .row0(displey_1__1), .row1(displey_1__2), .row2(displey_1__3), .row3(displey_1__4), .row4(displey_1__5),
    .row5(displey_1__6), .row6(displey_1__6_2));
  displey displey_1 (
    .in_2(lock), ._1(displey_1__1), ._2(displey_1__2), ._4(displey_1__4), ._3(displey_1__3),
    ._5(displey_1__5), ._6(displey_1__6), ._6_2(displey_1__6_2), .in_1(code));
  buf buffer_3 (buffer_3_out, buffer_3_out);
  DotMatrix #(.matrixrows(5)) dotmatrix_26 (
    .col0(draw_board_1_out_48_3), .col1(draw_board_1_out_48_2), .col2(draw_board_1_out_48[14:10]),
    .col3(draw_board_1_out_48[9:5]), .col4(draw_board_1_out_48[4:0]));
  DotMatrix #(.matrixrows(5)) dotmatrix_27 (
    .col0(draw_board_1_out_47_4), .col1(draw_board_1_out_47_3), .col2(draw_board_1_out_47_2),
    .col3(draw_board_1_out_47[9:5]), .col4(draw_board_1_out_47[4:0]));
  DotMatrix #(.matrixrows(5)) dotmatrix_28 (
    .col0(draw_board_1_out_46_4), .col1(draw_board_1_out_46_3), .col2(draw_board_1_out_46_2),
    .col3(draw_board_1_out_46[9:5]), .col4(draw_board_1_out_46[4:0]));
  DotMatrix #(.matrixrows(5)) dotmatrix_29 (
    .col0(draw_board_1_out_45_4), .col1(draw_board_1_out_45_3), .col2(draw_board_1_out_45_2),
    .col3(draw_board_1_out_45[9:5]), .col4(draw_board_1_out_45[4:0]));
  DotMatrix #(.matrixrows(5)) dotmatrix_30 (
    .col0(draw_board_1_out_44_4), .col1(draw_board_1_out_44_3), .col2(draw_board_1_out_44_2),
    .col3(draw_board_1_out_44[9:5]), .col4(draw_board_1_out_44[4:0]));
  DotMatrix #(.matrixrows(5)) dotmatrix_31 (
    .col0(draw_board_1_out_43_4), .col1(draw_board_1_out_43_3), .col2(draw_board_1_out_43_2),
    .col3(draw_board_1_out_43[9:5]), .col4(draw_board_1_out_43[4:0]));
  DotMatrix #(.matrixrows(5)) dotmatrix_32 (
    .col0(draw_board_1_out_42_4), .col1(draw_board_1_out_42_3), .col2(draw_board_1_out_42_2),
    .col3(draw_board_1_out_42[9:5]), .col4(draw_board_1_out_42[4:0]));
  DotMatrix #(.matrixrows(5)) dotmatrix_33 (
    .col0(draw_board_1_out_41_4), .col1(draw_board_1_out_41_3), .col2(draw_board_1_out_41_2),
    .col3(draw_board_1_out_41[9:5]), .col4(draw_board_1_out_41[4:0]));
  check_move check_move_1 (
    .from_letter(from_letter), .from_digit(from_digit), .to_letter(to_letter), .to_digit(to_digit),
    .enter(enter), .clock(clock), .out_14(from_line_output_hardware), .out_17(between_line_output_hardware),
    .out_18(to_line_output_hardware), .editing(editing), .counter(counter), .reset(reset),
    .possibly_move(possibly_move), .counter_cdm(counter_cdm), .ln1(ln1), .ln2(ln3), .ln3(ln2),
    .edit_cdm(code_reset), .\is_сapture (\is_сapture ));
  DotMatrix #(.matrixrows(5)) dotmatrix_34 (
    .col0(draw_board_1_out_56_3), .col1(draw_board_1_out_56_2), .col2(draw_board_1_out_56[14:10]),
    .col3(draw_board_1_out_56[9:5]), .col4(draw_board_1_out_56[4:0]));
  DotMatrix #(.matrixrows(5)) dotmatrix_35 (
    .col0(draw_board_1_out_64_3), .col1(draw_board_1_out_64_2), .col2(draw_board_1_out_64[14:10]),
    .col3(draw_board_1_out_64[9:5]), .col4(draw_board_1_out_64[4:0]));
  DotMatrix #(.matrixrows(5)) dotmatrix_36 (
    .col0(draw_board_1_out_63_4), .col1(draw_board_1_out_63_3), .col2(draw_board_1_out_63_2),
    .col3(draw_board_1_out_63[9:5]), .col4(draw_board_1_out_63[4:0]));
  DotMatrix #(.matrixrows(5)) dotmatrix_37 (
    .col0(draw_board_1_out_55_4), .col1(draw_board_1_out_55_3), .col2(draw_board_1_out_55_2),
    .col3(draw_board_1_out_55[9:5]), .col4(draw_board_1_out_55[4:0]));
  DotMatrix #(.matrixrows(5)) dotmatrix_38 (
    .col0(draw_board_1_out_54_4), .col1(draw_board_1_out_54_3), .col2(draw_board_1_out_54_2),
    .col3(draw_board_1_out_54[9:5]), .col4(draw_board_1_out_54[4:0]));
  DotMatrix #(.matrixrows(5)) dotmatrix_39 (
    .col0(draw_board_1_out_62_4), .col1(draw_board_1_out_62_3), .col2(draw_board_1_out_62_2),
    .col3(draw_board_1_out_62[9:5]), .col4(draw_board_1_out_62[4:0]));
  DotMatrix #(.matrixrows(5)) dotmatrix_40 (
    .col0(draw_board_1_out_53_4), .col1(draw_board_1_out_53_3), .col2(draw_board_1_out_53_2),
    .col3(draw_board_1_out_53[9:5]), .col4(draw_board_1_out_53[4:0]));
  DotMatrix #(.matrixrows(5)) dotmatrix_41 (
    .col0(draw_board_1_out_61_4), .col1(draw_board_1_out_61_3), .col2(draw_board_1_out_61_2),
    .col3(draw_board_1_out_61[9:5]), .col4(draw_board_1_out_61[4:0]));
  DotMatrix #(.matrixrows(5)) dotmatrix_42 (
    .col0(draw_board_1_out_52_4), .col1(draw_board_1_out_52_3), .col2(draw_board_1_out_52_2),
    .col3(draw_board_1_out_52[9:5]), .col4(draw_board_1_out_52[4:0]));
  DotMatrix #(.matrixrows(5)) dotmatrix_43 (
    .col0(draw_board_1_out_60_4), .col1(draw_board_1_out_60_3), .col2(draw_board_1_out_60_2),
    .col3(draw_board_1_out_60[9:5]), .col4(draw_board_1_out_60[4:0]));
  DotMatrix #(.matrixrows(5)) dotmatrix_44 (
    .col0(draw_board_1_out_51_4), .col1(draw_board_1_out_51_3), .col2(draw_board_1_out_51_2),
    .col3(draw_board_1_out_51[9:5]), .col4(draw_board_1_out_51[4:0]));
  DotMatrix #(.matrixrows(5)) dotmatrix_45 (
    .col0(draw_board_1_out_59_4), .col1(draw_board_1_out_59_3), .col2(draw_board_1_out_59_2),
    .col3(draw_board_1_out_59[9:5]), .col4(draw_board_1_out_59[4:0]));
  DotMatrix #(.matrixrows(5)) dotmatrix_46 (
    .col0(draw_board_1_out_50_4), .col1(draw_board_1_out_50_3), .col2(draw_board_1_out_50_2),
    .col3(draw_board_1_out_50[9:5]), .col4(draw_board_1_out_50[4:0]));
  DotMatrix #(.matrixrows(5)) dotmatrix_47 (
    .col0(draw_board_1_out_58_4), .col1(draw_board_1_out_58_3), .col2(draw_board_1_out_58_2),
    .col3(draw_board_1_out_58[9:5]), .col4(draw_board_1_out_58[4:0]));
  DotMatrix #(.matrixrows(5)) dotmatrix_48 (
    .col0(draw_board_1_out_57_4), .col1(draw_board_1_out_57_3), .col2(draw_board_1_out_57_2),
    .col3(draw_board_1_out_57[9:5]), .col4(draw_board_1_out_57[4:0]));
  DotMatrix #(.matrixrows(5)) dotmatrix_49 (
    .col0(draw_board_1_out_49_4), .col1(draw_board_1_out_49_3), .col2(draw_board_1_out_49_2),
    .col3(draw_board_1_out_49[9:5]), .col4(draw_board_1_out_49[4:0]));
  DotMatrix #(.matrixrows(5)) dotmatrix_50 (
    .col0(draw_board_1_out_72_3), .col1(draw_board_1_out_72_2), .col2(draw_board_1_out_72[14:10]),
    .col3(draw_board_1_out_72[9:5]), .col4(draw_board_1_out_72[4:0]));
  DotMatrix #(.matrixrows(5)) dotmatrix_51 (
    .col0(draw_board_1_out_71_4), .col1(draw_board_1_out_71_3), .col2(draw_board_1_out_71_2),
    .col3(draw_board_1_out_71[9:5]), .col4(draw_board_1_out_71[4:0]));
  DotMatrix #(.matrixrows(5)) dotmatrix_52 (
    .col0(draw_board_1_out_70_4), .col1(draw_board_1_out_70_3), .col2(draw_board_1_out_70_2),
    .col3(draw_board_1_out_70[9:5]), .col4(draw_board_1_out_70[4:0]));
  DotMatrix #(.matrixrows(5)) dotmatrix_53 (
    .col0(draw_board_1_out_69_4), .col1(draw_board_1_out_69_3), .col2(draw_board_1_out_69_2),
    .col3(draw_board_1_out_69[9:5]), .col4(draw_board_1_out_69[4:0]));
  DotMatrix #(.matrixrows(5)) dotmatrix_54 (
    .col0(draw_board_1_out_68_4), .col1(draw_board_1_out_68_3), .col2(draw_board_1_out_68_2),
    .col3(draw_board_1_out_68[9:5]), .col4(draw_board_1_out_68[4:0]));
  DotMatrix #(.matrixrows(5)) dotmatrix_55 (
    .col0(draw_board_1_out_67_4), .col1(draw_board_1_out_67_3), .col2(draw_board_1_out_67_2),
    .col3(draw_board_1_out_67[9:5]), .col4(draw_board_1_out_67[4:0]));
  DotMatrix #(.matrixrows(5)) dotmatrix_56 (
    .col0(draw_board_1_out_66_4), .col1(draw_board_1_out_66_3), .col2(draw_board_1_out_66_2),
    .col3(draw_board_1_out_66[9:5]), .col4(draw_board_1_out_66[4:0]));
  DotMatrix #(.matrixrows(5)) dotmatrix_57 (
    .col0(draw_board_1_out_65_4), .col1(draw_board_1_out_65_3), .col2(draw_board_1_out_65_2),
    .col3(draw_board_1_out_65[9:5]), .col4(draw_board_1_out_65[4:0]));
  find_between find_between_1 (.in_1(from_digit), .in_2(to_digit), .out_3(between_digit));
  DotMatrix #(.matrixrows(5)) dotmatrix_58 (
    .col0(draw_board_1_out_80_3), .col1(draw_board_1_out_80_2), .col2(draw_board_1_out_80[14:10]),
    .col3(draw_board_1_out_80[9:5]), .col4(draw_board_1_out_80[4:0]));
  DotMatrix #(.matrixrows(5)) dotmatrix_59 (
    .col0(draw_board_1_out_79_4), .col1(draw_board_1_out_79_3), .col2(draw_board_1_out_79_2),
    .col3(draw_board_1_out_79[9:5]), .col4(draw_board_1_out_79[4:0]));
  DotMatrix #(.matrixrows(5)) dotmatrix_60 (
    .col0(draw_board_1_out_78_4), .col1(draw_board_1_out_78_3), .col2(draw_board_1_out_78_2),
    .col3(draw_board_1_out_78[9:5]), .col4(draw_board_1_out_78[4:0]));
  DotMatrix #(.matrixrows(5)) dotmatrix_61 (
    .col0(draw_board_1_out_77_4), .col1(draw_board_1_out_77_3), .col2(draw_board_1_out_77_2),
    .col3(draw_board_1_out_77[9:5]), .col4(draw_board_1_out_77[4:0]));
  DotMatrix #(.matrixrows(5)) dotmatrix_62 (
    .col0(draw_board_1_out_76_4), .col1(draw_board_1_out_76_3), .col2(draw_board_1_out_76_2),
    .col3(draw_board_1_out_76[9:5]), .col4(draw_board_1_out_76[4:0]));
  DotMatrix #(.matrixrows(5)) dotmatrix_63 (
    .col0(draw_board_1_out_75_4), .col1(draw_board_1_out_75_3), .col2(draw_board_1_out_75_2),
    .col3(draw_board_1_out_75[9:5]), .col4(draw_board_1_out_75[4:0]));
  DotMatrix #(.matrixrows(5)) dotmatrix_64 (
    .col0(draw_board_1_out_74_4), .col1(draw_board_1_out_74_3), .col2(draw_board_1_out_74_2),
    .col3(draw_board_1_out_74[9:5]), .col4(draw_board_1_out_74[4:0]));
  DotMatrix #(.matrixrows(5)) dotmatrix_65 (
    .col0(draw_board_1_out_73_4), .col1(draw_board_1_out_73_3), .col2(draw_board_1_out_73_2),
    .col3(draw_board_1_out_73[9:5]), .col4(draw_board_1_out_73[4:0]));
  draw_board draw_board_1 (
    .in_9(demultiplexer_1_out0), .in_10(demultiplexer_1_out1), .in_11(demultiplexer_1_out2),
    .in_12(demultiplexer_1_out3), .in_13(demultiplexer_1_out4), .in_14(demultiplexer_1_out5),
    .in_15(demultiplexer_1_out6), .in_16(demultiplexer_1_out7), .in_1(coord_0_output), .in_2(coord_1_output),
    .in_3(coord_2_output), .in_4(coord_3_output), .in_5(coord_4_output), .in_6(coord_5_output),
    .in_7(coord_6_output), .in_8(coord_7_output),
    .out_24({draw_board_1_out_24_3, draw_board_1_out_24_2, draw_board_1_out_24}),
    .out_32({draw_board_1_out_32_3, draw_board_1_out_32_2, draw_board_1_out_32}),
    .out_40({draw_board_1_out_40_3, draw_board_1_out_40_2, draw_board_1_out_40}),
    .out_48({draw_board_1_out_48_3, draw_board_1_out_48_2, draw_board_1_out_48}),
    .out_56({draw_board_1_out_56_3, draw_board_1_out_56_2, draw_board_1_out_56}),
    .out_64({draw_board_1_out_64_3, draw_board_1_out_64_2, draw_board_1_out_64}),
    .out_72({draw_board_1_out_72_3, draw_board_1_out_72_2, draw_board_1_out_72}),
    .out_80({draw_board_1_out_80_3, draw_board_1_out_80_2, draw_board_1_out_80}),
    .out_18({draw_board_1_out_18_4, draw_board_1_out_18_3, draw_board_1_out_18_2, draw_board_1_out_18}),
    .out_26({draw_board_1_out_26_4, draw_board_1_out_26_3, draw_board_1_out_26_2, draw_board_1_out_26}),
    .out_34({draw_board_1_out_34_4, draw_board_1_out_34_3, draw_board_1_out_34_2, draw_board_1_out_34}),
    .out_42({draw_board_1_out_42_4, draw_board_1_out_42_3, draw_board_1_out_42_2, draw_board_1_out_42}),
    .out_50({draw_board_1_out_50_4, draw_board_1_out_50_3, draw_board_1_out_50_2, draw_board_1_out_50}),
    .out_58({draw_board_1_out_58_4, draw_board_1_out_58_3, draw_board_1_out_58_2, draw_board_1_out_58}),
    .out_66({draw_board_1_out_66_4, draw_board_1_out_66_3, draw_board_1_out_66_2, draw_board_1_out_66}),
    .out_74({draw_board_1_out_74_4, draw_board_1_out_74_3, draw_board_1_out_74_2, draw_board_1_out_74}),
    .out_19({draw_board_1_out_19_4, draw_board_1_out_19_3, draw_board_1_out_19_2, draw_board_1_out_19}),
    .out_27({draw_board_1_out_27_4, draw_board_1_out_27_3, draw_board_1_out_27_2, draw_board_1_out_27}),
    .out_35({draw_board_1_out_35_4, draw_board_1_out_35_3, draw_board_1_out_35_2, draw_board_1_out_35}),
    .out_43({draw_board_1_out_43_4, draw_board_1_out_43_3, draw_board_1_out_43_2, draw_board_1_out_43}),
    .out_51({draw_board_1_out_51_4, draw_board_1_out_51_3, draw_board_1_out_51_2, draw_board_1_out_51}),
    .out_59({draw_board_1_out_59_4, draw_board_1_out_59_3, draw_board_1_out_59_2, draw_board_1_out_59}),
    .out_67({draw_board_1_out_67_4, draw_board_1_out_67_3, draw_board_1_out_67_2, draw_board_1_out_67}),
    .out_75({draw_board_1_out_75_4, draw_board_1_out_75_3, draw_board_1_out_75_2, draw_board_1_out_75}),
    .out_20({draw_board_1_out_20_4, draw_board_1_out_20_3, draw_board_1_out_20_2, draw_board_1_out_20}),
    .out_28({draw_board_1_out_28_4, draw_board_1_out_28_3, draw_board_1_out_28_2, draw_board_1_out_28}),
    .out_36({draw_board_1_out_36_4, draw_board_1_out_36_3, draw_board_1_out_36_2, draw_board_1_out_36}),
    .out_44({draw_board_1_out_44_4, draw_board_1_out_44_3, draw_board_1_out_44_2, draw_board_1_out_44}),
    .out_52({draw_board_1_out_52_4, draw_board_1_out_52_3, draw_board_1_out_52_2, draw_board_1_out_52}),
    .out_60({draw_board_1_out_60_4, draw_board_1_out_60_3, draw_board_1_out_60_2, draw_board_1_out_60}),
    .out_68({draw_board_1_out_68_4, draw_board_1_out_68_3, draw_board_1_out_68_2, draw_board_1_out_68}),
    .out_76({draw_board_1_out_76_4, draw_board_1_out_76_3, draw_board_1_out_76_2, draw_board_1_out_76}),
    .out_21({draw_board_1_out_21_4, draw_board_1_out_21_3, draw_board_1_out_21_2, draw_board_1_out_21}),
    .out_29({draw_board_1_out_29_4, draw_board_1_out_29_3, draw_board_1_out_29_2, draw_board_1_out_29}),
    .out_37({draw_board_1_out_37_4, draw_board_1_out_37_3, draw_board_1_out_37_2, draw_board_1_out_37}),
    .out_45({draw_board_1_out_45_4, draw_board_1_out_45_3, draw_board_1_out_45_2, draw_board_1_out_45}),
    .out_53({draw_board_1_out_53_4, draw_board_1_out_53_3, draw_board_1_out_53_2, draw_board_1_out_53}),
    .out_61({draw_board_1_out_61_4, draw_board_1_out_61_3, draw_board_1_out_61_2, draw_board_1_out_61}),
    .out_69({draw_board_1_out_69_4, draw_board_1_out_69_3, draw_board_1_out_69_2, draw_board_1_out_69}),
    .out_77({draw_board_1_out_77_4, draw_board_1_out_77_3, draw_board_1_out_77_2, draw_board_1_out_77}),
    .out_22({draw_board_1_out_22_4, draw_board_1_out_22_3, draw_board_1_out_22_2, draw_board_1_out_22}),
    .out_30({draw_board_1_out_30_4, draw_board_1_out_30_3, draw_board_1_out_30_2, draw_board_1_out_30}),
    .out_38({draw_board_1_out_38_4, draw_board_1_out_38_3, draw_board_1_out_38_2, draw_board_1_out_38}),
    .out_46({draw_board_1_out_46_4, draw_board_1_out_46_3, draw_board_1_out_46_2, draw_board_1_out_46}),
    .out_54({draw_board_1_out_54_4, draw_board_1_out_54_3, draw_board_1_out_54_2, draw_board_1_out_54}),
    .out_62({draw_board_1_out_62_4, draw_board_1_out_62_3, draw_board_1_out_62_2, draw_board_1_out_62}),
    .out_70({draw_board_1_out_70_4, draw_board_1_out_70_3, draw_board_1_out_70_2, draw_board_1_out_70}),
    .out_78({draw_board_1_out_78_4, draw_board_1_out_78_3, draw_board_1_out_78_2, draw_board_1_out_78}),
    .out_23({draw_board_1_out_23_4, draw_board_1_out_23_3, draw_board_1_out_23_2, draw_board_1_out_23}),
    .out_31({draw_board_1_out_31_4, draw_board_1_out_31_3, draw_board_1_out_31_2, draw_board_1_out_31}),
    .out_39({draw_board_1_out_39_4, draw_board_1_out_39_3, draw_board_1_out_39_2, draw_board_1_out_39}),
    .out_47({draw_board_1_out_47_4, draw_board_1_out_47_3, draw_board_1_out_47_2, draw_board_1_out_47}),
    .out_55({draw_board_1_out_55_4, draw_board_1_out_55_3, draw_board_1_out_55_2, draw_board_1_out_55}),
    .out_63({draw_board_1_out_63_4, draw_board_1_out_63_3, draw_board_1_out_63_2, draw_board_1_out_63}),
    .out_71({draw_board_1_out_71_4, draw_board_1_out_71_3, draw_board_1_out_71_2, draw_board_1_out_71}),
    .out_79({draw_board_1_out_79_4, draw_board_1_out_79_3, draw_board_1_out_79_2, draw_board_1_out_79}),
    .out_17({draw_board_1_out_17_4, draw_board_1_out_17_3, draw_board_1_out_17_2, draw_board_1_out_17}),
    .out_25({draw_board_1_out_25_4, draw_board_1_out_25_3, draw_board_1_out_25_2, draw_board_1_out_25}),
    .out_33({draw_board_1_out_33_4, draw_board_1_out_33_3, draw_board_1_out_33_2, draw_board_1_out_33}),
    .out_41({draw_board_1_out_41_4, draw_board_1_out_41_3, draw_board_1_out_41_2, draw_board_1_out_41}),
    .out_49({draw_board_1_out_49_4, draw_board_1_out_49_3, draw_board_1_out_49_2, draw_board_1_out_49}),
    .out_57({draw_board_1_out_57_4, draw_board_1_out_57_3, draw_board_1_out_57_2, draw_board_1_out_57}),
    .out_65({draw_board_1_out_65_4, draw_board_1_out_65_3, draw_board_1_out_65_2, draw_board_1_out_65}),
    .out_73({draw_board_1_out_73_4, draw_board_1_out_73_3, draw_board_1_out_73_2, draw_board_1_out_73}));
  _7_Segment_Display u_7_segment_display_1 (
    .g(button_decoder_1_output_letter[3]), .f(button_decoder_1_output_letter[2]),
    .a(button_decoder_1_output_letter[1]), .b(button_decoder_1_output_letter[0]),
    .e(button_decoder_1_output_letter[7]), .d(button_decoder_1_output_letter[6]),
    .c(button_decoder_1_output_letter[5]), .dp(button_decoder_1_output_letter[4]));
  Button B (.out(B_out));
  Button A (.out(A_out));
  Button D (.out(D_out));
  Button C (.out(C_out));
  button_decoder button_decoder_1 (
    .output_digit({button_decoder_1_output_digit_2, button_decoder_1_output_digit}),
    .output_letter(button_decoder_1_output_letter), ._1(_1_out), .A(A_out), ._2(_2_out), .B(B_out),
    ._3(_3_out), .C(C_out), .D(D_out), ._5(_5_out), .E(E_out), ._6(_6_out), .F(F_out), ._7(_7_out),
    .G(G_out), ._8(_8_out), .H(H_out), .in_1(clock), .output_digit_number(from_digit),
    .output_letter_number(from_letter_t), .in_2(clear_button), .in_3(lock), ._4(_4_out));
  Button _1 (.out(_1_out));
  Button _3 (.out(_3_out));
  Button _2 (.out(_2_out));
  Button _4 (.out(_4_out));
  _7_Segment_Display u_7_segment_display_2 (
    .g(button_decoder_2_output_letter[3]), .f(button_decoder_2_output_letter[2]),
    .a(button_decoder_2_output_letter[1]), .b(button_decoder_2_output_letter[0]),
    .e(button_decoder_2_output_letter[7]), .d(button_decoder_2_output_letter[6]),
    .c(button_decoder_2_output_letter[5]), .dp(button_decoder_2_output_letter[4]));
  Button A_2 (.out(A_2_out));
  Button C_2 (.out(C_2_out));
  Button D_2 (.out(D_2_out));
  Button B_2 (.out(B_2_out));
  button_decoder button_decoder_2 (
    .output_digit({button_decoder_2_output_digit_2, button_decoder_2_output_digit}),
    .output_letter(button_decoder_2_output_letter), ._1(_1_2_out), .A(A_2_out), ._2(_2_2_out), .B(B_2_out),
    ._3(_3_2_out), .C(C_2_out), .D(D_2_out), ._5(_5_2_out), .E(E_2_out), ._6(_6_2_out), .F(F_2_out),
    ._7(_7_2_out), .G(G_2_out), ._8(_8_2_out), .H(H_2_out), .in_1(clock), .output_digit_number(to_digit),
    .output_letter_number(to_letter_t), .in_2(clear_button), .in_3(lock), ._4(_4_2_out));
  Button _2_2 (.out(_2_2_out));
  Button _3_2 (.out(_3_2_out));
  Button _4_2 (.out(_4_2_out));
  Button _1_2 (.out(_1_2_out));
  Button button_2 (.out(button_confirm));
  or or_9 (clear_button, counter_2_carry, code_reset);
  _7_Segment_Display u_7_segment_display_3 (
    .g(button_decoder_1_output_digit[3]), .f(button_decoder_1_output_digit[2]),
    .a(button_decoder_1_output_digit[1]), .b(button_decoder_1_output_digit[0]),
    .e(button_decoder_1_output_digit_2[3]), .d(button_decoder_1_output_digit_2[2]),
    .c(button_decoder_1_output_digit_2[1]), .dp(button_decoder_1_output_digit_2[0]));
  Button E (.out(E_out));
  Button H (.out(H_out));
  Button G (.out(G_out));
  Button F (.out(F_out));
  Button _5 (.out(_5_out));
  Button _6 (.out(_6_out));
  Button _8 (.out(_8_out));
  Button _7 (.out(_7_out));
  _7_Segment_Display u_7_segment_display_4 (
    .g(button_decoder_2_output_digit[3]), .f(button_decoder_2_output_digit[2]),
    .a(button_decoder_2_output_digit[1]), .b(button_decoder_2_output_digit[0]),
    .e(button_decoder_2_output_digit_2[3]), .d(button_decoder_2_output_digit_2[2]),
    .c(button_decoder_2_output_digit_2[1]), .dp(button_decoder_2_output_digit_2[0]));
  Button F_2 (.out(F_2_out));
  Button E_2 (.out(E_2_out));
  Button G_2 (.out(G_2_out));
  Button H_2 (.out(H_2_out));
  Button _5_2 (.out(_5_2_out));
  Button _7_2 (.out(_7_2_out));
  Button _8_2 (.out(_8_2_out));
  Button _6_2 (.out(_6_2_out));
  assign controlled_buffer_1_out = and_3_out ? clock : 1'bz;  // Controlled_Buffer controlled_buffer_1
  Counter #(.max('hf)) counter_2 (
    .carry(counter_2_carry), .clk(controlled_buffer_1_out), .clr(counter_2_carry));  // open: load, D, count, Q
  and and_3 (and_3_out, stop_editing, ~button_confirm);  // AND_Gate
  assign controlled_buffer_2_out = and_4_out ? clock : 1'bz;  // Controlled_Buffer controlled_buffer_2
  Counter #(.width(1), .max('h1), .ongoal("stay")) counter_3 (
    .Q(stop_editing), .clk(controlled_buffer_2_out), .clr(counter_2_carry));  // open: load, D, count, carry
  and and_4 (and_4_out, ~possibly_move, enter, ~lock, editing, ~button_confirm);  // AND_Gate

  // Notes on the sheet:
  //   Button Processing
  //   The difficulty level of the bot
  //   Screen Output Formatter
  //   8
  //   7
  //   6
  //   5
  //   4
  //   3
  //   2
  //   1
  //   A
  //   B
  //   C
  //   D
  //   E
  //   Move Processing Module
  //   G
  //   F
  //   H
  //   checker move from
  //   checker move to
  //   confirmation of the move
endmodule

module button_decoder (
  input  in_1,
  input  in_2,
  input  in_3,
  input  _1,
  input  _2,
  input  _3,
  input  _4,
  input  _5,
  input  _6,
  input  _7,
  input  _8,
  input  A,
  input  B,
  input  C,
  input  D,
  input  E,
  input  F,
  input  G,
  input  H,
  output [7:0] output_digit,
  output [7:0] output_digit_number,
  output [7:0] output_letter,
  output [7:0] output_letter_number
);

  wire and_1_out, and_2_out, or_2_out, or_3_out, pull_resistor_17_node, pull_resistor_18_node,
       pull_resistor_35_node, pull_resistor_36_node;
  wire [7:0] controlled_buffer_1_out, controlled_buffer_2_out, controlled_buffer_3_out,
       controlled_buffer_4_out, controlled_buffer_5_out, controlled_buffer_6_out, controlled_buffer_7_out,
       controlled_buffer_8_out, controlled_buffer_9_out, controlled_buffer_10_out, controlled_buffer_11_out,
       controlled_buffer_12_out, controlled_buffer_13_out, controlled_buffer_14_out,
       controlled_buffer_15_out, controlled_buffer_16_out, controlled_buffer_23_out,
       controlled_buffer_24_out, controlled_buffer_27_out, controlled_buffer_28_out,
       controlled_buffer_29_out, or_1_out, or_4_out, or_5_out, or_6_out, pull_resistor_19_node,
       pull_resistor_20_node, pull_resistor_21_node, pull_resistor_22_node, pull_resistor_25_node,
       pull_resistor_26_node, pull_resistor_30_node, pull_resistor_31_node, pull_resistor_32_node,
       pull_resistor_33_node, pull_resistor_34_node;

  assign controlled_buffer_1_out = _1 ? 8'h84 : 8'bz;  // Controlled_Buffer controlled_buffer_1
  assign controlled_buffer_2_out = _2 ? 8'hcb : 8'bz;  // Controlled_Buffer controlled_buffer_2
  assign controlled_buffer_3_out = _3 ? 8'h6b : 8'bz;  // Controlled_Buffer controlled_buffer_3
  assign controlled_buffer_4_out = _4 ? 8'h2d : 8'bz;  // Controlled_Buffer controlled_buffer_4
  assign controlled_buffer_5_out = _5 ? 8'h6e : 8'bz;  // Controlled_Buffer controlled_buffer_5
  assign controlled_buffer_6_out = _6 ? 8'hee : 8'bz;  // Controlled_Buffer controlled_buffer_6
  assign controlled_buffer_7_out = _7 ? 8'h23 : 8'bz;  // Controlled_Buffer controlled_buffer_7
  assign controlled_buffer_8_out = _8 ? 8'hef : 8'bz;  // Controlled_Buffer controlled_buffer_8
  assign controlled_buffer_9_out = A ? 8'haf : 8'bz;  // Controlled_Buffer controlled_buffer_9
  assign controlled_buffer_10_out = B ? 8'hec : 8'bz;  // Controlled_Buffer controlled_buffer_10
  assign controlled_buffer_11_out = C ? 8'hc6 : 8'bz;  // Controlled_Buffer controlled_buffer_11
  assign controlled_buffer_12_out = D ? 8'he9 : 8'bz;  // Controlled_Buffer controlled_buffer_12
  assign controlled_buffer_13_out = E ? 8'hce : 8'bz;  // Controlled_Buffer controlled_buffer_13
  assign controlled_buffer_14_out = F ? 8'h8e : 8'bz;  // Controlled_Buffer controlled_buffer_14
  assign controlled_buffer_15_out = G ? 8'hfe : 8'bz;  // Controlled_Buffer controlled_buffer_15
  assign controlled_buffer_16_out = H ? 8'had : 8'bz;  // Controlled_Buffer controlled_buffer_16
  Pull_Resistor pull_resistor_1 (.node(controlled_buffer_1_out));
  Pull_Resistor pull_resistor_2 (.node(controlled_buffer_2_out));
  Pull_Resistor pull_resistor_3 (.node(controlled_buffer_3_out));
  Pull_Resistor pull_resistor_4 (.node(controlled_buffer_4_out));
  Pull_Resistor pull_resistor_5 (.node(controlled_buffer_5_out));
  Pull_Resistor pull_resistor_6 (.node(controlled_buffer_6_out));
  Pull_Resistor pull_resistor_7 (.node(controlled_buffer_7_out));
  Pull_Resistor pull_resistor_8 (.node(controlled_buffer_8_out));
  Pull_Resistor pull_resistor_9 (.node(controlled_buffer_9_out));
  Pull_Resistor pull_resistor_10 (.node(controlled_buffer_10_out));
  Pull_Resistor pull_resistor_11 (.node(controlled_buffer_11_out));
  Pull_Resistor pull_resistor_12 (.node(controlled_buffer_12_out));
  Pull_Resistor pull_resistor_13 (.node(controlled_buffer_13_out));
  Pull_Resistor pull_resistor_14 (.node(controlled_buffer_14_out));
  Pull_Resistor pull_resistor_15 (.node(controlled_buffer_15_out));
  Pull_Resistor pull_resistor_16 (.node(controlled_buffer_16_out));
  assign or_1_out = controlled_buffer_1_out | controlled_buffer_2_out | controlled_buffer_3_out | controlled_buffer_4_out | controlled_buffer_5_out | controlled_buffer_6_out | controlled_buffer_7_out | controlled_buffer_8_out;  // OR_Gate or_1, 8 bits wide
  Pull_Resistor pull_resistor_17 (.node(pull_resistor_17_node));
  assign pull_resistor_17_node = and_1_out ? in_1 : 1'bz;  // Controlled_Buffer controlled_buffer_17
  and and_1 (and_1_out, ~in_3, or_2_out);  // AND_Gate
  or or_2 (or_2_out, _1, _2, _3, _4, _5, _6, _7, _8);
  or or_3 (or_3_out, A, B, C, D, E, F, G, H);
  Register register_1 (.D(or_1_out), .Q(output_digit), .clk(pull_resistor_17_node), .clr(in_2));  // open: en
  assign or_4_out = controlled_buffer_9_out | controlled_buffer_10_out | controlled_buffer_11_out | controlled_buffer_12_out | controlled_buffer_13_out | controlled_buffer_14_out | controlled_buffer_15_out | controlled_buffer_16_out;  // OR_Gate or_4, 8 bits wide
  and and_2 (and_2_out, ~in_3, or_3_out);  // AND_Gate
  Register register_2 (.D(or_4_out), .Q(output_letter), .clk(pull_resistor_18_node), .clr(in_2));  // open: en
  Pull_Resistor pull_resistor_18 (.node(pull_resistor_18_node));
  assign pull_resistor_18_node = and_2_out ? in_1 : 1'bz;  // Controlled_Buffer controlled_buffer_18
  Pull_Resistor pull_resistor_19 (.node(pull_resistor_19_node));
  assign pull_resistor_19_node = _1 ? {8{1'b0}} : 8'bz;  // Controlled_Buffer controlled_buffer_19
  Pull_Resistor pull_resistor_20 (.node(pull_resistor_20_node));
  assign pull_resistor_20_node = _2 ? 8'h1 : 8'bz;  // Controlled_Buffer controlled_buffer_20
  Pull_Resistor pull_resistor_21 (.node(pull_resistor_21_node));
  assign pull_resistor_21_node = _3 ? 8'h2 : 8'bz;  // Controlled_Buffer controlled_buffer_21
  Pull_Resistor pull_resistor_22 (.node(pull_resistor_22_node));
  assign pull_resistor_22_node = _4 ? 8'h3 : 8'bz;  // Controlled_Buffer controlled_buffer_22
  assign controlled_buffer_23_out = _5 ? 8'h4 : 8'bz;  // Controlled_Buffer controlled_buffer_23
  Pull_Resistor pull_resistor_23 (.node(controlled_buffer_23_out));
  assign controlled_buffer_24_out = _6 ? 8'h5 : 8'bz;  // Controlled_Buffer controlled_buffer_24
  Pull_Resistor pull_resistor_24 (.node(controlled_buffer_24_out));
  Pull_Resistor pull_resistor_25 (.node(pull_resistor_25_node));
  assign pull_resistor_25_node = _7 ? 8'h6 : 8'bz;  // Controlled_Buffer controlled_buffer_25
  Pull_Resistor pull_resistor_26 (.node(pull_resistor_26_node));
  assign pull_resistor_26_node = _8 ? 8'h7 : 8'bz;  // Controlled_Buffer controlled_buffer_26
  assign controlled_buffer_27_out = A ? {8{1'b0}} : 8'bz;  // Controlled_Buffer controlled_buffer_27
  Pull_Resistor pull_resistor_27 (.node(controlled_buffer_27_out));
  assign controlled_buffer_28_out = B ? 8'h1 : 8'bz;  // Controlled_Buffer controlled_buffer_28
  Pull_Resistor pull_resistor_28 (.node(controlled_buffer_28_out));
  assign controlled_buffer_29_out = C ? 8'h2 : 8'bz;  // Controlled_Buffer controlled_buffer_29
  Pull_Resistor pull_resistor_29 (.node(controlled_buffer_29_out));
  Pull_Resistor pull_resistor_30 (.node(pull_resistor_30_node));
  assign pull_resistor_30_node = D ? 8'h3 : 8'bz;  // Controlled_Buffer controlled_buffer_30
  Pull_Resistor pull_resistor_31 (.node(pull_resistor_31_node));
  assign pull_resistor_31_node = E ? 8'h4 : 8'bz;  // Controlled_Buffer controlled_buffer_31
  Pull_Resistor pull_resistor_32 (.node(pull_resistor_32_node));
  assign pull_resistor_32_node = F ? 8'h5 : 8'bz;  // Controlled_Buffer controlled_buffer_32
  Pull_Resistor pull_resistor_33 (.node(pull_resistor_33_node));
  assign pull_resistor_33_node = G ? 8'h6 : 8'bz;  // Controlled_Buffer controlled_buffer_33
  Pull_Resistor pull_resistor_34 (.node(pull_resistor_34_node));
  assign pull_resistor_34_node = H ? 8'h7 : 8'bz;  // Controlled_Buffer controlled_buffer_34
  Register register_3 (.D(or_5_out), .Q(output_digit_number), .clk(pull_resistor_35_node), .clr(in_2));  // open: en
  assign or_5_out = pull_resistor_19_node | pull_resistor_20_node | pull_resistor_21_node | pull_resistor_22_node | controlled_buffer_23_out | controlled_buffer_24_out | pull_resistor_25_node | pull_resistor_26_node;  // OR_Gate or_5, 8 bits wide
  Pull_Resistor pull_resistor_35 (.node(pull_resistor_35_node));
  assign pull_resistor_35_node = and_1_out ? in_1 : 1'bz;  // Controlled_Buffer controlled_buffer_35
  assign or_6_out = controlled_buffer_27_out | controlled_buffer_28_out | controlled_buffer_29_out | pull_resistor_30_node | pull_resistor_31_node | pull_resistor_32_node | pull_resistor_33_node | pull_resistor_34_node;  // OR_Gate or_6, 8 bits wide
  Register register_4 (.D(or_6_out), .Q(output_letter_number), .clk(pull_resistor_36_node), .clr(in_2));  // open: en
  Pull_Resistor pull_resistor_36 (.node(pull_resistor_36_node));
  assign pull_resistor_36_node = and_2_out ? in_1 : 1'bz;  // Controlled_Buffer controlled_buffer_36

  // Other names for the same wires on the sheet: button_digit_1 = _1; button_digit_2 = _2; button_digit_3 = _3;
  //   button_digit_4 = _4; button_digit_5 = _5; button_digit_6 = _6; button_digit_7 = _7; button_digit_8 = _8;
  //   button_letter_A = A; button_letter_B = B; button_letter_C = C; button_letter_D = D; button_letter_E = E;
  //   button_letter_F = F; button_letter_G = G; button_letter_H = H; clock = in_1; lock = in_3; reset = in_2
endmodule

module draw_board (
  input  [24:0] in_1,
  input  [24:0] in_2,
  input  [24:0] in_3,
  input  [24:0] in_4,
  input  [24:0] in_5,
  input  [24:0] in_6,
  input  [24:0] in_7,
  input  [24:0] in_8,
  input  in_9,
  input  in_10,
  input  in_11,
  input  in_12,
  input  in_13,
  input  in_14,
  input  in_15,
  input  in_16,
  output [24:0] out_17,
  output [24:0] out_18,
  output [24:0] out_19,
  output [24:0] out_20,
  output [24:0] out_21,
  output [24:0] out_22,
  output [24:0] out_23,
  output [24:0] out_24,
  output [24:0] out_25,
  output [24:0] out_26,
  output [24:0] out_27,
  output [24:0] out_28,
  output [24:0] out_29,
  output [24:0] out_30,
  output [24:0] out_31,
  output [24:0] out_32,
  output [24:0] out_33,
  output [24:0] out_34,
  output [24:0] out_35,
  output [24:0] out_36,
  output [24:0] out_37,
  output [24:0] out_38,
  output [24:0] out_39,
  output [24:0] out_40,
  output [24:0] out_41,
  output [24:0] out_42,
  output [24:0] out_43,
  output [24:0] out_44,
  output [24:0] out_45,
  output [24:0] out_46,
  output [24:0] out_47,
  output [24:0] out_48,
  output [24:0] out_49,
  output [24:0] out_50,
  output [24:0] out_51,
  output [24:0] out_52,
  output [24:0] out_53,
  output [24:0] out_54,
  output [24:0] out_55,
  output [24:0] out_56,
  output [24:0] out_57,
  output [24:0] out_58,
  output [24:0] out_59,
  output [24:0] out_60,
  output [24:0] out_61,
  output [24:0] out_62,
  output [24:0] out_63,
  output [24:0] out_64,
  output [24:0] out_65,
  output [24:0] out_66,
  output [24:0] out_67,
  output [24:0] out_68,
  output [24:0] out_69,
  output [24:0] out_70,
  output [24:0] out_71,
  output [24:0] out_72,
  output [24:0] out_73,
  output [24:0] out_74,
  output [24:0] out_75,
  output [24:0] out_76,
  output [24:0] out_77,
  output [24:0] out_78,
  output [24:0] out_79,
  output [24:0] out_80
);

  variable_25 variable_25_1 (.\input (in_1), .\output (out_17), .clock(in_9));
  variable_25 variable_25_2 (.\input (in_2), .\output (out_25), .clock(in_9));
  variable_25 variable_25_3 (.\input (in_3), .\output (out_33), .clock(in_9));
  variable_25 variable_25_4 (.\input (in_4), .\output (out_41), .clock(in_9));
  variable_25 variable_25_5 (.\input (in_5), .\output (out_49), .clock(in_9));
  variable_25 variable_25_6 (.\input (in_6), .\output (out_57), .clock(in_9));
  variable_25 variable_25_7 (.\input (in_7), .\output (out_65), .clock(in_9));
  variable_25 variable_25_8 (.\input (in_8), .\output (out_73), .clock(in_9));
  variable_25 variable_25_9 (.\input (in_1), .\output (out_18), .clock(in_10));
  variable_25 variable_25_10 (.\input (in_2), .\output (out_26), .clock(in_10));
  variable_25 variable_25_11 (.\input (in_3), .\output (out_34), .clock(in_10));
  variable_25 variable_25_12 (.\input (in_4), .\output (out_42), .clock(in_10));
  variable_25 variable_25_13 (.\input (in_5), .\output (out_50), .clock(in_10));
  variable_25 variable_25_14 (.\input (in_6), .\output (out_58), .clock(in_10));
  variable_25 variable_25_15 (.\input (in_7), .\output (out_66), .clock(in_10));
  variable_25 variable_25_16 (.\input (in_8), .\output (out_74), .clock(in_10));
  variable_25 variable_25_17 (.\input (in_1), .\output (out_19), .clock(in_11));
  variable_25 variable_25_18 (.\input (in_2), .\output (out_27), .clock(in_11));
  variable_25 variable_25_19 (.\input (in_3), .\output (out_35), .clock(in_11));
  variable_25 variable_25_20 (.\input (in_4), .\output (out_43), .clock(in_11));
  variable_25 variable_25_21 (.\input (in_5), .\output (out_51), .clock(in_11));
  variable_25 variable_25_22 (.\input (in_6), .\output (out_59), .clock(in_11));
  variable_25 variable_25_23 (.\input (in_7), .\output (out_67), .clock(in_11));
  variable_25 variable_25_24 (.\input (in_8), .\output (out_75), .clock(in_11));
  variable_25 variable_25_25 (.\input (in_1), .\output (out_20), .clock(in_12));
  variable_25 variable_25_26 (.\input (in_2), .\output (out_28), .clock(in_12));
  variable_25 variable_25_27 (.\input (in_3), .\output (out_36), .clock(in_12));
  variable_25 variable_25_28 (.\input (in_4), .\output (out_44), .clock(in_12));
  variable_25 variable_25_29 (.\input (in_5), .\output (out_52), .clock(in_12));
  variable_25 variable_25_30 (.\input (in_6), .\output (out_60), .clock(in_12));
  variable_25 variable_25_31 (.\input (in_7), .\output (out_68), .clock(in_12));
  variable_25 variable_25_32 (.\input (in_8), .\output (out_76), .clock(in_12));
  variable_25 variable_25_33 (.\input (in_1), .\output (out_21), .clock(in_13));
  variable_25 variable_25_34 (.\input (in_2), .\output (out_29), .clock(in_13));
  variable_25 variable_25_35 (.\input (in_3), .\output (out_37), .clock(in_13));
  variable_25 variable_25_36 (.\input (in_4), .\output (out_45), .clock(in_13));
  variable_25 variable_25_37 (.\input (in_5), .\output (out_53), .clock(in_13));
  variable_25 variable_25_38 (.\input (in_6), .\output (out_61), .clock(in_13));
  variable_25 variable_25_39 (.\input (in_7), .\output (out_69), .clock(in_13));
  variable_25 variable_25_40 (.\input (in_8), .\output (out_77), .clock(in_13));
  variable_25 variable_25_41 (.\input (in_1), .\output (out_22), .clock(in_14));
  variable_25 variable_25_42 (.\input (in_2), .\output (out_30), .clock(in_14));
  variable_25 variable_25_43 (.\input (in_3), .\output (out_38), .clock(in_14));
  variable_25 variable_25_44 (.\input (in_4), .\output (out_46), .clock(in_14));
  variable_25 variable_25_45 (.\input (in_5), .\output (out_54), .clock(in_14));
  variable_25 variable_25_46 (.\input (in_6), .\output (out_62), .clock(in_14));
  variable_25 variable_25_47 (.\input (in_7), .\output (out_70), .clock(in_14));
  variable_25 variable_25_48 (.\input (in_8), .\output (out_78), .clock(in_14));
  variable_25 variable_25_49 (.\input (in_1), .\output (out_23), .clock(in_15));
  variable_25 variable_25_50 (.\input (in_2), .\output (out_31), .clock(in_15));
  variable_25 variable_25_51 (.\input (in_3), .\output (out_39), .clock(in_15));
  variable_25 variable_25_52 (.\input (in_4), .\output (out_47), .clock(in_15));
  variable_25 variable_25_53 (.\input (in_5), .\output (out_55), .clock(in_15));
  variable_25 variable_25_54 (.\input (in_6), .\output (out_63), .clock(in_15));
  variable_25 variable_25_55 (.\input (in_7), .\output (out_71), .clock(in_15));
  variable_25 variable_25_56 (.\input (in_8), .\output (out_79), .clock(in_15));
  variable_25 variable_25_57 (.\input (in_1), .\output (out_24), .clock(in_16));
  variable_25 variable_25_58 (.\input (in_2), .\output (out_32), .clock(in_16));
  variable_25 variable_25_59 (.\input (in_3), .\output (out_40), .clock(in_16));
  variable_25 variable_25_60 (.\input (in_4), .\output (out_48), .clock(in_16));
  variable_25 variable_25_61 (.\input (in_5), .\output (out_56), .clock(in_16));
  variable_25 variable_25_62 (.\input (in_6), .\output (out_64), .clock(in_16));
  variable_25 variable_25_63 (.\input (in_7), .\output (out_72), .clock(in_16));
  variable_25 variable_25_64 (.\input (in_8), .\output (out_80), .clock(in_16));

  // Other names for the same wires on the sheet: coord_0_output[24:0] = in_1; coord_1_output[24:0] = in_2;
  //   coord_2_output[24:0] = in_3; coord_3_output[24:0] = in_4; coord_4_output[24:0] = in_5;
  //   coord_5_output[24:0] = in_6; coord_6_output[24:0] = in_7; coord_7_output[24:0] = in_8
endmodule

module coord_convert (
  input  [3:0] in_1,
  input  [3:0] in_2,
  input  [3:0] in_3,
  input  [3:0] in_4,
  input  [3:0] in_5,
  input  [3:0] in_6,
  input  [3:0] in_7,
  input  [3:0] in_8,
  input  in_9,
  input  in_10,
  output [24:0] out_11,
  output [24:0] out_12,
  output [24:0] out_13,
  output [24:0] out_14,
  output [24:0] out_15,
  output [24:0] out_16,
  output [24:0] out_17,
  output [24:0] out_18
);

  checkers_piece checkers_piece_1 (.in_3(in_1), .out_4(out_11), .x1(in_9), .x2(in_10));
  checkers_piece checkers_piece_2 (.in_3(in_3), .out_4(out_13), .x1(in_9), .x2(in_10));
  checkers_piece checkers_piece_3 (.in_3(in_5), .out_4(out_15), .x1(in_9), .x2(in_10));
  checkers_piece checkers_piece_4 (.in_3(in_7), .out_4(out_17), .x1(in_9), .x2(in_10));
  checkers_piece checkers_piece_5 (.in_3(in_2), .out_4(out_12), .x1(in_10), .x2(in_9));
  checkers_piece checkers_piece_6 (.in_3(in_4), .out_4(out_14), .x1(in_10), .x2(in_9));
  checkers_piece checkers_piece_7 (.in_3(in_6), .out_4(out_16), .x1(in_10), .x2(in_9));
  checkers_piece checkers_piece_8 (.in_3(in_8), .out_4(out_18), .x1(in_10), .x2(in_9));

  // Other names for the same wires on the sheet: _2k1_bin = in_10; _2k_bin = in_9
endmodule

module find_between (
  input  [7:0] in_1,
  input  [7:0] in_2,
  output [7:0] out_3
);

  wire comparator_1_gt, comparator_1_lt;
  wire [7:0] controlled_buffer_1_out, controlled_buffer_2_out, or_1_out, subtractor_1_out;

  Subtractor subtractor_1 (.a(in_1), .b(in_2), .out(subtractor_1_out));  // open: bin, bout
  Comparator comparator_1 (
    .a(subtractor_1_out), .b({8{1'b0}}), .gt(comparator_1_gt), .lt(comparator_1_lt));  // open: eq
  assign controlled_buffer_1_out = comparator_1_lt ? {8{1'b1}} : 8'bz;  // Controlled_Buffer controlled_buffer_1
  Pull_Resistor pull_resistor_1 (.node(controlled_buffer_1_out));
  assign or_1_out = controlled_buffer_1_out | controlled_buffer_2_out;  // OR_Gate or_1, 8 bits wide
  assign controlled_buffer_2_out = comparator_1_gt ? 8'h1 : 8'bz;  // Controlled_Buffer controlled_buffer_2
  Pull_Resistor pull_resistor_2 (.node(controlled_buffer_2_out));
  Subtractor subtractor_2 (.a(in_1), .b(or_1_out), .out(out_3));  // open: bin, bout

  // Other names for the same wires on the sheet: from[7:0] = in_1; to[7:0] = in_2
endmodule

module variable_25 (
  input  [24:0] \input ,
  input  clock,
  output [24:0] \output 
);

  Register #(.width(25), .trigger("falling")) register_1 (.D(\input ), .Q(\output ), .clk(clock));  // open: en, clr
endmodule

module varieble_32 (
  input  [31:0] \input ,
  input  clock,
  output [31:0] \output 
);

  Register #(.width(32)) register_1 (.D(\input ), .Q(\output ), .clk(clock));  // open: en, clr
endmodule

module variable_16 (
  input  [15:0] \input ,
  input  clock,
  output [15:0] \output 
);

  Register #(.width(16), .trigger("high")) register_1 (.D(\input ), .Q(\output ), .clk(clock));  // open: en, clr
endmodule

module white_black_log (
  input  input_x1,
  input  [24:0] \input ,
  input  input_x2,
  output [24:0] \output 
);

  wire and_1_out, comparator_1_eq, comparator_1_gt, comparator_1_lt, or_1_out, or_2_out;
  wire [24:0] and_2_out, controlled_buffer_1_out, controlled_buffer_2_out, controlled_buffer_3_out,
       not_1_out, not_2_out;

  Comparator #(.width(25)) comparator_1 (
    .a({25{1'b0}}), .b(\input ), .gt(comparator_1_gt), .eq(comparator_1_eq), .lt(comparator_1_lt));
  or or_1 (or_1_out, input_x2, or_2_out);
  assign controlled_buffer_1_out = or_1_out ? \input  : 25'bz;  // Controlled_Buffer controlled_buffer_1
  and and_1 (and_1_out, comparator_1_eq, input_x1);
  or or_2 (or_2_out, comparator_1_lt, comparator_1_gt);
  assign controlled_buffer_2_out = and_1_out ? \input  : 25'bz;  // Controlled_Buffer controlled_buffer_2
  assign controlled_buffer_3_out = and_1_out ? \input  : 25'bz;  // Controlled_Buffer controlled_buffer_3
  Pull_Resistor pull_resistor_1 (.node(controlled_buffer_2_out));
  Pull_Resistor #(.pull(1)) pull_resistor_2 (.node(controlled_buffer_3_out));
  Pull_Resistor pull_resistor_3 (.node(controlled_buffer_1_out));
  assign not_1_out = ~controlled_buffer_2_out;  // NOT_Gate not_1, 25 bits wide
  assign and_2_out = not_1_out & not_2_out;  // AND_Gate and_2, 25 bits wide
  assign not_2_out = ~controlled_buffer_3_out;  // NOT_Gate not_2, 25 bits wide
  assign \output  = and_2_out | controlled_buffer_1_out;  // OR_Gate or_3, 25 bits wide
endmodule

module checkers_piece (
  input  x1,
  input  x2,
  input  [3:0] in_3,
  output [24:0] out_4
);

  wire [24:0] rom_1_data;

  Pull_Resistor pull_resistor_1 (.node(in_3));
  ROM #(.addrWidth(4), .dataWidth(25)) rom_1 (.addr(in_3), .data(rom_1_data));  // open: sel
  white_black_log white_black_log_1 (.\input (rom_1_data), .\output (out_4), .input_x2(x1), .input_x1(x2));

  // Notes on the sheet:
  //   contents of rom_1 (hex, n*v repeats v):
  //   0 1f8d63f 729c0 1b8923b 476dc4
endmodule

module map (
  input  [7:0] from_index,
  input  [7:0] between_index,
  input  [7:0] to_index,
  input  [31:0] overwriting_input,
  input  [31:0] overwriting_input_2,
  input  [31:0] overwriting_input_3,
  input  [1:0] counter,
  input  editing,
  input  reset,
  input  clock,
  output [7:0] out_11,
  output [31:0] out_12,
  output out_13
);

  wire and_2_out, and_3_out, and_4_out, comparator_1_eq, controlled_buffer_1_out, counter_2_q, counter_5_q,
       last_line, nor_1_out, not_1_out, not_2_out, not_3_out, not_4_out, or_1_out, or_3_out,
       possibility_overwriting, reset_counter;
  wire [7:0] controlled_buffer_2_out, counter_4_q, pull_resistor_1_node, transistor_1_out;
  wire [31:0] multiplexer_2_out, or_2_out, pull_resistor_2_node, pull_resistor_3_node;

  not not_1 (not_1_out, not_1_out);
  Comparator #(.width(2)) comparator_1 (.a(counter), .b(2'b11), .eq(comparator_1_eq));  // open: gt, lt
  not not_2 (not_2_out, not_2_out);
  Counter #(.width(2), .max('h2)) counter_1 (
    .carry(reset_counter), .clk(comparator_1_eq), .clr(or_1_out));  // open: load, D, count, Q
  or or_1 (or_1_out, last_line, reset);
  not not_3 (not_3_out, not_3_out);
  Counter #(.width(1), .max('h1)) counter_2 (
    .Q(counter_2_q), .clk(last_line), .clr(reset_counter));  // open: load, D, count, carry
  Pull_Resistor pull_resistor_1 (.node(pull_resistor_1_node));
  Multiplexer #(.select(2), .width(8), .enable("false")) multiplexer_1 (
    .in0(from_index), .in1(between_index), .in2(to_index), .in3({8{1'b1}}), .out(pull_resistor_1_node),
    .sel(counter));
  and and_1 (possibility_overwriting, counter_2_q, ~out_13);  // AND_Gate
  and and_2 (and_2_out, ~counter_2_q, ~out_13);  // AND_Gate
  Counter counter_3 (.Q(out_11), .clk(controlled_buffer_1_out), .clr(last_line));  // open: load, D, count, carry
  assign controlled_buffer_1_out = nor_1_out ? clock : 1'bz;  // Controlled_Buffer controlled_buffer_1
  nor nor_1 (nor_1_out, out_13, counter_2_q);
  assign controlled_buffer_2_out = possibility_overwriting ? pull_resistor_1_node : 8'bz;  // Controlled_Buffer controlled_buffer_2
  assign controlled_buffer_2_out = and_2_out ? out_11 : 8'bz;  // Controlled_Buffer controlled_buffer_3
  assign controlled_buffer_2_out = out_13 ? transistor_1_out : 8'bz;  // Controlled_Buffer controlled_buffer_4
  Comparator #(.mode("unsigned")) comparator_2 (.a(out_11), .b(8'h7), .gt(last_line));  // open: eq, lt
  Transistor #(.\type ("n"), .gate("br"), .width(8)) transistor_1 (
    .in(counter_4_q), .out(transistor_1_out), .gate(out_13));
  Counter counter_4 (.Q(counter_4_q), .clk(and_3_out));  // open: load, D, count, carry, clr
  Counter #(.width(1), .max('h1)) counter_5 (.Q(counter_5_q), .clk(not_4_out));  // open: load, D, count, carry, clr
  and and_3 (and_3_out, clock, ~counter_5_q);  // AND_Gate
  Comparator #(.mode("unsigned")) comparator_3 (.a(counter_4_q), .b(8'h8), .lt(out_13));  // open: gt, eq
  not not_4 (not_4_out, out_13);
  assign or_2_out = pull_resistor_2_node | pull_resistor_3_node;  // OR_Gate or_2, 32 bits wide
  Pull_Resistor pull_resistor_2 (.node(pull_resistor_2_node));
  ROM #(.dataWidth(32)) rom_1 (.addr(transistor_1_out), .data(pull_resistor_2_node));  // open: sel
  Pull_Resistor pull_resistor_3 (.node(pull_resistor_3_node));
  or or_3 (or_3_out, out_13, and_4_out);
  and and_4 (and_4_out, editing, possibility_overwriting);
  assign pull_resistor_3_node = possibility_overwriting ? multiplexer_2_out : 32'bz;  // Controlled_Buffer controlled_buffer_5
  RAM #(.dataWidth(32), .bus("separate")) ram_1 (
    .addr(controlled_buffer_2_out), .din(or_2_out), .data(out_12), .str(or_3_out), .sel(1'b1), .clk(clock),
    .ld(1'b1), .clr(1'b0));
  Multiplexer #(.select(2), .width(32), .enable("false")) multiplexer_2 (
    .in0(overwriting_input), .in1(overwriting_input_2), .in2(overwriting_input_3), .in3({32{1'b1}}),
    .out(multiplexer_2_out), .sel(counter));

  // Other names for the same wires on the sheet: between_line_output[31:0] = overwriting_input_2;
  //   from_line_output[31:0] = overwriting_input; to_line_output[31:0] = overwriting_input_3

  // Notes on the sheet:
  //   Move Data I/O Module
  //   Auto-Reset Counter
  //   RAM Initialization and Overwrite Module
  //   contents of rom_1 (hex, n*v repeats v):
  //   2020202 20202020 2020202 0 0 10101010 1010101 10101010
endmodule

module check_move (
  input  [15:0] ln1,
  input  [7:0] from_letter,
  input  [7:0] from_digit,
  input  [7:0] to_letter,
  input  [15:0] ln2,
  input  [7:0] to_digit,
  input  [15:0] ln3,
  input  enter,
  input  [1:0] counter_cdm,
  input  clock,
  input  edit_cdm,
  input  reset,
  input  \is_сapture ,
  output [31:0] out_14,
  output editing,
  output [1:0] counter,
  output [31:0] out_17,
  output [31:0] out_18,
  output possibly_move
);

  wire and_1_out, and_3_out, and_5_out, and_6_out, and_7_out, and_8_out, buffer_1_out, buffer_2_out,
       buffer_3_out, buffer_4_out, capture, comparator_1_eq, comparator_2_eq, comparator_3_eq,
       comparator_4_eq, comparator_5_eq, comparator_6_eq, comparator_7_eq, comparator_8_eq, comparator_9_eq,
       comparator_10_eq, comparator_11_eq, comparator_12_eq, controlled_buffer_13_out,
       controlled_buffer_14_out, controlled_buffer_15_out, controlled_buffer_20_out, counter_1_carry,
       counter_2_q, demultiplexer_2_out1, demultiplexer_2_out2, demultiplexer_2_out3, demultiplexer_3_out0,
       demultiplexer_3_out1, demultiplexer_3_out2, demultiplexer_3_out3, demultiplexer_3_out4,
       demultiplexer_3_out5, demultiplexer_3_out6, demultiplexer_3_out7, demultiplexer_4_out0,
       demultiplexer_4_out1, demultiplexer_4_out2, demultiplexer_4_out3, demultiplexer_4_out4,
       demultiplexer_4_out5, demultiplexer_4_out6, demultiplexer_4_out7, move, not_1_out, not_2_out,
       not_3_out, not_4_out, not_5_out, not_6_out, not_7_out, not_8_out, not_9_out, not_10_out, not_11_out,
       not_12_out, not_13_out, not_14_out, not_15_out, not_16_out, not_17_out, not_18_out, not_19_out,
       not_20_out, or_1_out, or_2_out, or_9_out, or_10_out, or_11_out, or_12_out, or_13_out, or_15_out,
       or_16_out, or_17_out, or_18_out, or_19_out, pull_resistor_20_node, pull_resistor_21_node;
  wire [1:0] or_7_out;
  wire [2:0] bit_extender_2_out, bit_extender_3_out, bit_extender_4_out, bit_extender_5_out,
       bit_extender_6_out, bit_extender_7_out, counter_1_q;
  wire [3:0] controlled_buffer_17_out, controlled_buffer_18_out, controlled_buffer_22_out,
       controlled_buffer_23_out, controlled_buffer_29_out, controlled_buffer_34_out,
       controlled_buffer_36_out, controlled_buffer_38_out, demultiplexer_5_out0, demultiplexer_5_out1,
       demultiplexer_5_out2, demultiplexer_5_out3, demultiplexer_5_out4, demultiplexer_5_out5,
       demultiplexer_5_out6, demultiplexer_5_out7, man, multiplexer_2_out, multiplexer_3_out,
       multiplexer_4_out, or_20_out, pull_resistor_25_node, pull_resistor_28_node, pull_resistor_29_node,
       pull_resistor_30_node, pull_resistor_31_node, pull_resistor_32_node, pull_resistor_34_node,
       pull_resistor_35_node, pull_resistor_37_node, pull_resistor_39_node, pull_resistor_41_node;
  wire [7:0] between_digit, between_letter, controlled_buffer_3_out, controlled_buffer_7_out,
       controlled_buffer_8_out, controlled_buffer_9_out, controlled_buffer_10_out, controlled_buffer_12_out,
       index_1, index_2, index_3, multiplier_1_out, multiplier_2_out, multiplier_3_out, multiplier_4_cout,
       multiplier_4_out, multiplier_5_out, or_6_out, or_8_out, or_14_out, pull_resistor_1_node,
       pull_resistor_2_node, pull_resistor_4_node, pull_resistor_5_node, pull_resistor_6_node,
       pull_resistor_11_node, subtractor_1_out, subtractor_2_out, subtractor_3_out, subtractor_4_out,
       subtractor_5_out, subtractor_6_out;
  wire [31:0] between_line, between_line_ans, controlled_buffer_30_out, controlled_buffer_31_out,
       controlled_buffer_40_out, controlled_buffer_41_out, controlled_buffer_42_out,
       controlled_buffer_43_out, demultiplexer_1_out2, demultiplexer_1_out3, from_line, from_line_ans,
       line_1, line_2, line_3, map_1_out_12, or_21_out, pull_resistor_13_node, to_line, to_line_ans;

  buf buffer_1 (buffer_1_out, buffer_1_out);
  buf buffer_2 (buffer_2_out, buffer_2_out);
  find_between find_between_1 (.in_1(from_digit), .in_2(to_digit), .out_3(between_digit));
  find_between find_between_2 (.in_1(from_letter), .in_2(to_letter), .out_3(between_letter));
  Pull_Resistor pull_resistor_1 (.node(pull_resistor_1_node));
  assign pull_resistor_1_node = enter ? to_digit : 8'bz;  // Controlled_Buffer controlled_buffer_1
  Subtractor subtractor_1 (
    .a(pull_resistor_1_node), .b(pull_resistor_2_node), .out(subtractor_1_out));  // open: bin, bout
  Pull_Resistor pull_resistor_2 (.node(pull_resistor_2_node));
  assign pull_resistor_2_node = enter ? from_digit : 8'bz;  // Controlled_Buffer controlled_buffer_2
  assign controlled_buffer_3_out = enter ? to_digit : 8'bz;  // Controlled_Buffer controlled_buffer_3
  Pull_Resistor pull_resistor_3 (.node(controlled_buffer_3_out));
  Subtractor subtractor_2 (
    .a(controlled_buffer_3_out), .b(pull_resistor_4_node), .out(subtractor_2_out));  // open: bin, bout
  Pull_Resistor pull_resistor_4 (.node(pull_resistor_4_node));
  assign pull_resistor_4_node = enter ? from_digit : 8'bz;  // Controlled_Buffer controlled_buffer_4
  Pull_Resistor pull_resistor_5 (.node(pull_resistor_5_node));
  assign pull_resistor_5_node = enter ? from_letter : 8'bz;  // Controlled_Buffer controlled_buffer_5
  Pull_Resistor pull_resistor_6 (.node(pull_resistor_6_node));
  assign pull_resistor_6_node = enter ? to_letter : 8'bz;  // Controlled_Buffer controlled_buffer_6
  Multiplier multiplier_1 (.a(subtractor_1_out), .b(subtractor_1_out), .out(multiplier_1_out));  // open: cin, cout
  Subtractor subtractor_3 (
    .a(pull_resistor_5_node), .b(pull_resistor_6_node), .out(subtractor_3_out));  // open: bin, bout
  Multiplier multiplier_2 (.a(subtractor_3_out), .b(subtractor_3_out), .out(multiplier_2_out));  // open: cin, cout
  Comparator comparator_1 (.a(multiplier_1_out), .b(8'h1), .eq(comparator_1_eq));  // open: gt, lt
  and and_1 (and_1_out, comparator_1_eq, comparator_2_eq);
  Comparator #(.width(4)) comparator_2 (.a(man), .b(4'b0100), .eq(comparator_2_eq));  // open: gt, lt
  Comparator comparator_3 (.a(subtractor_2_out), .b(8'h1), .eq(comparator_3_eq));  // open: gt, lt
  Comparator #(.mode("unsigned")) comparator_4 (.a(8'h1), .b(multiplier_2_out), .eq(comparator_4_eq));  // open: gt, lt
  or or_1 (or_1_out, and_1_out, comparator_3_eq);
  and and_2 (move, ~\is_сapture , or_1_out, comparator_4_eq);  // AND_Gate
  assign controlled_buffer_7_out = enter ? from_digit : 8'bz;  // Controlled_Buffer controlled_buffer_7
  Pull_Resistor pull_resistor_7 (.node(controlled_buffer_7_out));
  assign controlled_buffer_8_out = enter ? to_digit : 8'bz;  // Controlled_Buffer controlled_buffer_8
  Pull_Resistor pull_resistor_8 (.node(controlled_buffer_8_out));
  assign controlled_buffer_9_out = enter ? to_digit : 8'bz;  // Controlled_Buffer controlled_buffer_9
  Pull_Resistor pull_resistor_9 (.node(controlled_buffer_9_out));
  assign controlled_buffer_10_out = enter ? from_digit : 8'bz;  // Controlled_Buffer controlled_buffer_10
  Pull_Resistor pull_resistor_10 (.node(controlled_buffer_10_out));
  Pull_Resistor pull_resistor_11 (.node(pull_resistor_11_node));
  assign pull_resistor_11_node = enter ? from_letter : 8'bz;  // Controlled_Buffer controlled_buffer_11
  assign controlled_buffer_12_out = enter ? to_letter : 8'bz;  // Controlled_Buffer controlled_buffer_12
  Pull_Resistor pull_resistor_12 (.node(controlled_buffer_12_out));
  Subtractor subtractor_4 (
    .a(controlled_buffer_7_out), .b(controlled_buffer_8_out), .out(subtractor_4_out));  // open: bin, bout
  Multiplier multiplier_3 (.a(subtractor_4_out), .b(subtractor_4_out), .out(multiplier_3_out));  // open: cin, cout
  Subtractor subtractor_5 (
    .a(controlled_buffer_9_out), .b(controlled_buffer_10_out), .out(subtractor_5_out));  // open: bin, bout
  Subtractor subtractor_6 (
    .a(pull_resistor_11_node), .b(controlled_buffer_12_out), .out(subtractor_6_out));  // open: bin, bout
  parsing_data parsing_data_1 (.in_1(ln1), .out_3(line_1), .out_2(index_1));
  parsing_data parsing_data_2 (.in_1(ln2), .out_3(line_2), .out_2(index_2));
  parsing_data parsing_data_3 (.in_1(ln3), .out_3(line_3), .out_2(index_3));
  Comparator comparator_5 (.a(multiplier_3_out), .b(multiplier_4_out), .eq(comparator_5_eq));  // open: gt, lt
  Comparator #(.width(4)) comparator_6 (.a(man), .b(4'b0100), .eq(comparator_6_eq));  // open: gt, lt
  Comparator comparator_7 (.a(subtractor_5_out), .b(8'h2), .eq(comparator_7_eq));  // open: gt, lt
  Multiplier multiplier_4 (.a(8'h2), .b(8'h2), .out(multiplier_4_out), .cout(multiplier_4_cout));  // open: cin
  Comparator #(.mode("unsigned")) comparator_8 (
    .a(multiplier_4_out), .b(multiplier_5_out), .eq(comparator_8_eq));  // open: gt, lt
  Multiplier multiplier_5 (
    .a(subtractor_6_out), .b(subtractor_6_out), .out(multiplier_5_out), .cin(multiplier_4_cout));  // open: cout
  and and_3 (and_3_out, comparator_5_eq, comparator_6_eq);
  or or_2 (or_2_out, and_3_out, comparator_7_eq);
  and and_4 (capture, or_2_out, comparator_8_eq);
  buf buffer_3 (buffer_3_out, buffer_3_out);
  Pull_Resistor pull_resistor_13 (.node(pull_resistor_13_node));
  varieble_32 varieble_32_1 (.\input (pull_resistor_13_node), .\output (from_line), .clock(or_10_out));
  assign from_line_ans = line_1 | out_14;  // OR_Gate or_3, 32 bits wide
  assign between_line_ans = line_2 | out_17;  // OR_Gate or_4, 32 bits wide
  assign to_line_ans = line_3 | out_18;  // OR_Gate or_5, 32 bits wide
  assign or_6_out = from_digit | index_1;  // OR_Gate or_6, 8 bits wide
  Demultiplexer #(.select(2), .width(32)) demultiplexer_1 (
    .out1(pull_resistor_13_node), .out2(demultiplexer_1_out2), .out3(demultiplexer_1_out3),
    .in(map_1_out_12), .sel(or_7_out), .en(counter_2_q));  // open: out0
  Pull_Resistor pull_resistor_14 (.node(demultiplexer_1_out2));
  Pull_Resistor pull_resistor_15 (.node(demultiplexer_1_out3));
  varieble_32 varieble_32_2 (.\input (demultiplexer_1_out2), .\output (between_line), .clock(or_11_out));
  varieble_32 varieble_32_3 (.\input (demultiplexer_1_out3), .\output (to_line), .clock(or_12_out));
  assign or_7_out = counter_cdm | counter;  // OR_Gate or_7, 2 bits wide
  assign or_8_out = between_digit | index_2;  // OR_Gate or_8, 8 bits wide
  or or_9 (or_9_out, possibly_move, edit_cdm);
  or or_10 (or_10_out, controlled_buffer_15_out, demultiplexer_2_out1);
  or or_11 (or_11_out, controlled_buffer_15_out, demultiplexer_2_out2);
  or or_12 (or_12_out, controlled_buffer_15_out, demultiplexer_2_out3);
  Counter #(.width(3), .max('h3)) counter_1 (
    .Q(counter_1_q), .carry(counter_1_carry), .clk(controlled_buffer_13_out), .clr(or_15_out));  // open: load, D, count
  and and_5 (and_5_out, ~counter_1_carry, or_13_out);  // AND_Gate
  or or_13 (or_13_out, editing, counter_2_q);
  assign controlled_buffer_13_out = and_5_out ? clock : 1'bz;  // Controlled_Buffer controlled_buffer_13
  assign or_14_out = index_3 | to_digit;  // OR_Gate or_14, 8 bits wide
  map map_1 (
    .clock(clock), .out_12(map_1_out_12), .from_index(or_6_out), .to_index(or_14_out),
    .between_index(or_8_out), .overwriting_input(from_line_ans), .counter(or_7_out), .editing(or_9_out),
    .reset(reset), .overwriting_input_2(between_line_ans), .overwriting_input_3(to_line_ans));  // open: out_11, out_13
  Demultiplexer #(.select(2)) demultiplexer_2 (
    .out1(demultiplexer_2_out1), .out2(demultiplexer_2_out2), .out3(demultiplexer_2_out3), .in(1'b1),
    .sel(or_7_out), .en(counter_2_q));  // open: out0
  Pull_Resistor pull_resistor_16 (.node(demultiplexer_2_out1));
  Pull_Resistor pull_resistor_17 (.node(demultiplexer_2_out2));
  Pull_Resistor pull_resistor_18 (.node(demultiplexer_2_out3));
  Bit_Extender #(.in_width(3), .out_width(2), .\type ("sign")) bit_extender_1 (.in(counter_1_q), .out(counter));
  and and_6 (and_6_out, editing, counter_2_q);
  or or_15 (or_15_out, and_6_out, reset);
  Counter #(.width(1), .max('h1)) counter_2 (
    .Q(counter_2_q), .clk(or_16_out), .clr(or_17_out));  // open: load, D, count, carry
  or or_16 (or_16_out, enter, counter_2_q);
  assign controlled_buffer_14_out = and_7_out ? clock : 1'bz;  // Controlled_Buffer controlled_buffer_14
  and and_7 (and_7_out, ~editing, counter_1_carry);  // AND_Gate
  or or_17 (or_17_out, reset, editing);
  assign controlled_buffer_15_out = reset ? clock : 1'bz;  // Controlled_Buffer controlled_buffer_15
  Pull_Resistor pull_resistor_19 (.node(controlled_buffer_15_out));
  Counter #(.width(1), .max('h1)) counter_3 (
    .Q(editing), .clk(controlled_buffer_14_out), .clr(reset));  // open: load, D, count, carry
  buf buffer_4 (buffer_4_out, buffer_4_out);
  Bit_Extender #(.out_width(3), .\type ("sign")) bit_extender_2 (.in(from_letter), .out(bit_extender_2_out));
  Bit_Extender #(.out_width(3), .\type ("sign")) bit_extender_3 (.in(from_letter), .out(bit_extender_3_out));
  Multiplexer #(.select(3), .width(4), .enable("false")) multiplexer_1 (
    .in0(from_line[3:0]), .in1(from_line[7:4]), .in2(from_line[11:8]), .in3(from_line[15:12]),
    .in4(from_line[19:16]), .in5(from_line[23:20]), .in6(from_line[27:24]), .in7(from_line[31:28]),
    .out(man), .sel(bit_extender_3_out));
  Bit_Extender #(.out_width(3), .\type ("sign")) bit_extender_4 (.in(between_letter), .out(bit_extender_4_out));
  Multiplexer #(.select(3), .width(4), .enable("false")) multiplexer_2 (
    .in0(between_line[3:0]), .in1(between_line[7:4]), .in2(between_line[11:8]), .in3(between_line[15:12]),
    .in4(between_line[19:16]), .in5(between_line[23:20]), .in6(between_line[27:24]),
    .in7(between_line[31:28]), .out(multiplexer_2_out), .sel(bit_extender_4_out));
  Bit_Extender #(.out_width(3), .\type ("sign")) bit_extender_5 (.in(to_letter), .out(bit_extender_5_out));
  Multiplexer #(.select(3), .width(4), .enable("false")) multiplexer_3 (
    .in0(to_line[3:0]), .in1(to_line[7:4]), .in2(to_line[11:8]), .in3(to_line[15:12]), .in4(to_line[19:16]),
    .in5(to_line[23:20]), .in6(to_line[27:24]), .in7(to_line[31:28]), .out(multiplexer_3_out),
    .sel(bit_extender_5_out));
  Multiplexer #(.select(3), .width(4), .enable("false")) multiplexer_4 (
    .in0(from_line[3:0]), .in1(from_line[7:4]), .in2(from_line[11:8]), .in3(from_line[15:12]),
    .in4(from_line[19:16]), .in5(from_line[23:20]), .in6(from_line[27:24]), .in7(from_line[31:28]),
    .out(multiplexer_4_out), .sel(bit_extender_2_out));
  Comparator #(.width(4)) comparator_9 (.a(4'b0100), .b(man), .eq(comparator_9_eq));  // open: gt, lt
  Comparator #(.width(4)) comparator_10 (.a(man), .b(4'b0010), .eq(comparator_10_eq));  // open: gt, lt
  or or_18 (or_18_out, move, capture);
  Comparator #(.width(4)) comparator_11 (.a(4'b0000), .b(multiplexer_3_out), .eq(comparator_11_eq));  // open: gt, lt
  Bit_Extender #(.out_width(3), .\type ("sign")) bit_extender_6 (.in(between_letter), .out(bit_extender_6_out));
  Pull_Resistor pull_resistor_20 (.node(pull_resistor_20_node));
  Demultiplexer #(.select(3), .enable("false")) demultiplexer_3 (
    .out0(demultiplexer_3_out0), .out1(demultiplexer_3_out1), .out2(demultiplexer_3_out2),
    .out3(demultiplexer_3_out3), .out4(demultiplexer_3_out4), .out5(demultiplexer_3_out5),
    .out6(demultiplexer_3_out6), .out7(demultiplexer_3_out7), .in(pull_resistor_20_node),
    .sel(bit_extender_6_out));
  assign pull_resistor_20_node = and_8_out ? 1'b1 : 1'bz;  // Controlled_Buffer controlled_buffer_16
  and and_8 (and_8_out, editing, possibly_move, capture);
  Bit_Extender #(.out_width(3), .\type ("sign")) bit_extender_7 (.in(to_letter), .out(bit_extender_7_out));
  Comparator comparator_12 (.a(to_digit), .b(8'h7), .eq(comparator_12_eq));  // open: gt, lt
  assign controlled_buffer_17_out = comparator_12_eq ? 4'b0100 : 4'bz;  // Controlled_Buffer controlled_buffer_17
  assign controlled_buffer_18_out = not_1_out ? multiplexer_4_out : 4'bz;  // Controlled_Buffer controlled_buffer_18
  not not_1 (not_1_out, comparator_12_eq);
  or or_19 (or_19_out, comparator_9_eq, comparator_10_eq);
  and and_9 (possibly_move, or_19_out, or_18_out, editing, pull_resistor_21_node, comparator_11_eq);
  Pull_Resistor #(.pull(1)) pull_resistor_21 (.node(pull_resistor_21_node));
  assign pull_resistor_21_node = capture ? multiplexer_2_out[0] : 1'bz;  // Controlled_Buffer controlled_buffer_19
  not not_2 (not_2_out, demultiplexer_3_out0);
  not not_3 (not_3_out, demultiplexer_3_out1);
  not not_4 (not_4_out, demultiplexer_3_out2);
  not not_5 (not_5_out, demultiplexer_3_out3);
  not not_6 (not_6_out, demultiplexer_3_out4);
  not not_7 (not_7_out, demultiplexer_3_out5);
  not not_8 (not_8_out, demultiplexer_3_out6);
  not not_9 (not_9_out, demultiplexer_3_out7);
  Pull_Resistor pull_resistor_22 (.node(controlled_buffer_17_out));
  assign or_20_out = controlled_buffer_17_out | controlled_buffer_18_out;  // OR_Gate or_20, 4 bits wide
  Pull_Resistor pull_resistor_23 (.node(controlled_buffer_18_out));
  Demultiplexer #(.select(3), .enable("false")) demultiplexer_4 (
    .out0(demultiplexer_4_out0), .out1(demultiplexer_4_out1), .out2(demultiplexer_4_out2),
    .out3(demultiplexer_4_out3), .out4(demultiplexer_4_out4), .out5(demultiplexer_4_out5),
    .out6(demultiplexer_4_out6), .out7(demultiplexer_4_out7), .in(controlled_buffer_20_out),
    .sel(bit_extender_3_out));
  assign controlled_buffer_20_out = possibly_move ? 1'b1 : 1'bz;  // Controlled_Buffer controlled_buffer_20
  Pull_Resistor pull_resistor_24 (.node(controlled_buffer_20_out));
  Pull_Resistor pull_resistor_25 (.node(pull_resistor_25_node));
  Demultiplexer #(.select(3), .width(4), .enable("false")) demultiplexer_5 (
    .out0(demultiplexer_5_out0), .out1(demultiplexer_5_out1), .out2(demultiplexer_5_out2),
    .out3(demultiplexer_5_out3), .out4(demultiplexer_5_out4), .out5(demultiplexer_5_out5),
    .out6(demultiplexer_5_out6), .out7(demultiplexer_5_out7), .in(pull_resistor_25_node),
    .sel(bit_extender_7_out));
  assign pull_resistor_25_node = possibly_move ? or_20_out : 4'bz;  // Controlled_Buffer controlled_buffer_21
  not not_10 (not_10_out, demultiplexer_4_out0);
  not not_11 (not_11_out, demultiplexer_4_out1);
  not not_12 (not_12_out, demultiplexer_4_out2);
  not not_13 (not_13_out, demultiplexer_4_out3);
  not not_14 (not_14_out, demultiplexer_4_out4);
  not not_15 (not_15_out, demultiplexer_4_out5);
  not not_16 (not_16_out, demultiplexer_4_out6);
  not not_17 (not_17_out, demultiplexer_4_out7);
  assign controlled_buffer_22_out = not_2_out ? between_line[3:0] : 4'bz;  // Controlled_Buffer controlled_buffer_22
  Pull_Resistor pull_resistor_26 (.node(controlled_buffer_22_out));
  assign controlled_buffer_23_out = not_3_out ? between_line[7:4] : 4'bz;  // Controlled_Buffer controlled_buffer_23
  Pull_Resistor pull_resistor_27 (.node(controlled_buffer_23_out));
  Pull_Resistor pull_resistor_28 (.node(pull_resistor_28_node));
  assign pull_resistor_28_node = not_4_out ? between_line[11:8] : 4'bz;  // Controlled_Buffer controlled_buffer_24
  Pull_Resistor pull_resistor_29 (.node(pull_resistor_29_node));
  assign pull_resistor_29_node = not_5_out ? between_line[15:12] : 4'bz;  // Controlled_Buffer controlled_buffer_25
  Pull_Resistor pull_resistor_30 (.node(pull_resistor_30_node));
  assign pull_resistor_30_node = not_6_out ? between_line[19:16] : 4'bz;  // Controlled_Buffer controlled_buffer_26
  Pull_Resistor pull_resistor_31 (.node(pull_resistor_31_node));
  assign pull_resistor_31_node = not_7_out ? between_line[23:20] : 4'bz;  // Controlled_Buffer controlled_buffer_27
  Pull_Resistor pull_resistor_32 (.node(pull_resistor_32_node));
  assign pull_resistor_32_node = not_8_out ? between_line[27:24] : 4'bz;  // Controlled_Buffer controlled_buffer_28
  assign controlled_buffer_29_out = not_9_out ? between_line[31:28] : 4'bz;  // Controlled_Buffer controlled_buffer_29
  Pull_Resistor pull_resistor_33 (.node(controlled_buffer_29_out));
  assign controlled_buffer_30_out = and_8_out ? {controlled_buffer_29_out, pull_resistor_32_node, pull_resistor_31_node, pull_resistor_30_node, pull_resistor_29_node, pull_resistor_28_node, controlled_buffer_23_out, controlled_buffer_22_out} : 32'bz;  // Controlled_Buffer controlled_buffer_30
  assign controlled_buffer_31_out = possibly_move ? or_21_out : 32'bz;  // Controlled_Buffer controlled_buffer_31
  assign or_21_out = {demultiplexer_5_out7, demultiplexer_5_out6, demultiplexer_5_out5, demultiplexer_5_out4, demultiplexer_5_out3, demultiplexer_5_out2, demultiplexer_5_out1, demultiplexer_5_out0} | to_line;  // OR_Gate or_21, 32 bits wide
  Pull_Resistor pull_resistor_34 (.node(pull_resistor_34_node));
  assign pull_resistor_34_node = not_10_out ? from_line[3:0] : 4'bz;  // Controlled_Buffer controlled_buffer_32
  Pull_Resistor pull_resistor_35 (.node(pull_resistor_35_node));
  assign pull_resistor_35_node = not_11_out ? from_line[7:4] : 4'bz;  // Controlled_Buffer controlled_buffer_33
  assign controlled_buffer_34_out = not_12_out ? from_line[11:8] : 4'bz;  // Controlled_Buffer controlled_buffer_34
  Pull_Resistor pull_resistor_36 (.node(controlled_buffer_34_out));
  Pull_Resistor pull_resistor_37 (.node(pull_resistor_37_node));
  assign pull_resistor_37_node = not_13_out ? from_line[15:12] : 4'bz;  // Controlled_Buffer controlled_buffer_35
  assign controlled_buffer_36_out = not_14_out ? from_line[19:16] : 4'bz;  // Controlled_Buffer controlled_buffer_36
  Pull_Resistor pull_resistor_38 (.node(controlled_buffer_36_out));
  Pull_Resistor pull_resistor_39 (.node(pull_resistor_39_node));
  assign pull_resistor_39_node = not_15_out ? from_line[23:20] : 4'bz;  // Controlled_Buffer controlled_buffer_37
  assign controlled_buffer_38_out = not_16_out ? from_line[27:24] : 4'bz;  // Controlled_Buffer controlled_buffer_38
  Pull_Resistor pull_resistor_40 (.node(controlled_buffer_38_out));
  Pull_Resistor pull_resistor_41 (.node(pull_resistor_41_node));
  assign pull_resistor_41_node = not_17_out ? from_line[31:28] : 4'bz;  // Controlled_Buffer controlled_buffer_39
  Pull_Resistor pull_resistor_42 (.node(controlled_buffer_30_out));
  assign controlled_buffer_40_out = not_18_out ? between_line : 32'bz;  // Controlled_Buffer controlled_buffer_40
  Pull_Resistor pull_resistor_43 (.node(controlled_buffer_40_out));
  not not_18 (not_18_out, and_8_out);
  Pull_Resistor pull_resistor_44 (.node(controlled_buffer_31_out));
  assign out_18 = controlled_buffer_31_out | controlled_buffer_41_out;  // OR_Gate or_22, 32 bits wide
  assign controlled_buffer_41_out = not_19_out ? to_line : 32'bz;  // Controlled_Buffer controlled_buffer_41
  Pull_Resistor pull_resistor_45 (.node(controlled_buffer_41_out));
  not not_19 (not_19_out, possibly_move);
  assign controlled_buffer_42_out = possibly_move ? {pull_resistor_41_node, controlled_buffer_38_out, pull_resistor_39_node, controlled_buffer_36_out, pull_resistor_37_node, controlled_buffer_34_out, pull_resistor_35_node, pull_resistor_34_node} : 32'bz;  // Controlled_Buffer controlled_buffer_42
  not not_20 (not_20_out, possibly_move);
  assign out_17 = controlled_buffer_30_out | controlled_buffer_40_out;  // OR_Gate or_23, 32 bits wide
  Pull_Resistor pull_resistor_46 (.node(controlled_buffer_42_out));
  assign out_14 = controlled_buffer_42_out | controlled_buffer_43_out;  // OR_Gate or_24, 32 bits wide
  assign controlled_buffer_43_out = not_20_out ? from_line : 32'bz;  // Controlled_Buffer controlled_buffer_43
  Pull_Resistor pull_resistor_47 (.node(controlled_buffer_43_out));

  // Other names for the same wires on the sheet: between_line_output[31:0] = out_17; from_line_output[31:0] = out_14;
  //   to_line_output[31:0] = out_18

  // Notes on the sheet:
  //   Move Data I/O Module
  //   Move Logic Module
  //   Memory Read/Write Module
  //   Move Processing and Output Module
endmodule

module signa_extension (
  input  button,
  input  clock,
  output reset,
  output enter
);

  wire and_1_out, and_2_out, controlled_buffer_1_out, controlled_buffer_2_out, counter_1_q, counter_3_carry,
       signa_extension_rev_1_out_5;

  signa_extension_rev signa_extension_rev_1 (
    .reset(reset), .\input (counter_1_q), .clock(clock), .out_5(signa_extension_rev_1_out_5), .button(button));
  Counter #(.width(1), .max('h1)) counter_1 (
    .Q(counter_1_q), .clk(counter_3_carry), .clr(signa_extension_rev_1_out_5));  // open: load, D, count, carry
  and and_1 (and_1_out, button, ~enter);  // AND_Gate
  Counter #(.width(1), .max('h1)) counter_2 (
    .Q(enter), .clk(controlled_buffer_1_out), .clr(counter_3_carry));  // open: load, D, count, carry
  assign controlled_buffer_1_out = and_1_out ? clock : 1'bz;  // Controlled_Buffer controlled_buffer_1
  Counter #(.width(3), .max('h7)) counter_3 (
    .carry(counter_3_carry), .clk(controlled_buffer_2_out), .clr(counter_3_carry));  // open: load, D, count, Q
  assign controlled_buffer_2_out = and_2_out ? clock : 1'bz;  // Controlled_Buffer controlled_buffer_2
  and and_2 (and_2_out, enter, ~button);  // AND_Gate
endmodule

module signa_extension_rev (
  input  \input ,
  input  button,
  input  clock,
  output reset,
  output out_5
);

  wire and_1_out, controlled_buffer_1_out, controlled_buffer_2_out, controlled_buffer_3_out, not_1_out;

  Counter #(.width(1), .max('h1)) counter_1 (
    .Q(reset), .clk(controlled_buffer_1_out), .clr(out_5));  // open: load, D, count, carry
  assign controlled_buffer_1_out = and_1_out ? controlled_buffer_3_out : 1'bz;  // Controlled_Buffer controlled_buffer_1
  and and_1 (and_1_out, \input , ~reset);  // AND_Gate
  not not_1 (not_1_out, button);
  Counter #(.width(3), .max('h7)) counter_2 (
    .carry(out_5), .clk(controlled_buffer_2_out), .clr(out_5));  // open: load, D, count, Q
  assign controlled_buffer_2_out = reset ? controlled_buffer_3_out : 1'bz;  // Controlled_Buffer controlled_buffer_2
  assign controlled_buffer_3_out = not_1_out ? clock : 1'bz;  // Controlled_Buffer controlled_buffer_3
endmodule

module CDM (
  input  reset,
  input  [3:0] in_2,
  input  [15:0] Y1,
  input  [15:0] X1,
  input  [15:0] Y2,
  input  [15:0] X2,
  input  CLCK,
  output [3:0] CODE,
  output [15:0] LINE3,
  output [15:0] LINE2,
  output [15:0] LINE1
);

  wire and_1_out, and_2_out, cdm_16_1_p5, cdm_16_1_p6, cdm_16_1_p7, cdm_16_1_p9, cdm_16_1_p10, cdm_16_1_p11,
       cdm_16_1_p12, comparator_1_eq, comparator_2_eq, comparator_3_eq, comparator_4_eq, comparator_5_eq,
       Isel, mem, not_1_out, not_2_out, or_1_out, or_2_out, RAM, read, word;
  wire [3:0] cdm_16_1_p8, divider_1_out;
  wire [15:0] addr, cdm_16_1_p2, cdm_16_1_p4, cdm_16_1_p17, cdm_16_1_p18, controlled_buffer_2_out,
       controlled_buffer_3_out, controlled_buffer_4_out, controlled_buffer_5_out, controlled_buffer_6_out,
       data, undriven;
  wire [15:4] cdm_16_1_p8_2;

  // Debugger debugger_1: pin names not known
  Pull_Resistor pull_resistor_1 (.node(CODE));
  Pull_Resistor pull_resistor_2 (.node(reset));
  variable_16 variable_16_1 (.\input (controlled_buffer_2_out), .\output (LINE3), .clock(or_2_out));
  variable_16 variable_16_2 (.\input (controlled_buffer_3_out), .\output (LINE2), .clock(or_2_out));
  variable_16 variable_16_3 (.\input (controlled_buffer_4_out), .\output (LINE1), .clock(or_2_out));
  assign CODE = and_1_out ? cdm_16_1_p8 : 4'bz;  // Controlled_Buffer controlled_buffer_1
  Comparator #(.width(4)) comparator_1 (.a(CODE), .b(4'b0110), .eq(comparator_1_eq));  // open: gt, lt
  and and_1 (and_1_out, cdm_16_1_p8_2[4], cdm_16_1_p8_2[5], cdm_16_1_p8_2[6], cdm_16_1_p8_2[7], cdm_16_1_p8_2[8], cdm_16_1_p8_2[9], cdm_16_1_p8_2[10], cdm_16_1_p8_2[11], cdm_16_1_p8_2[12], cdm_16_1_p8_2[13], cdm_16_1_p8_2[14], ~cdm_16_1_p8_2[15], 1'b1);  // AND_Gate
  or or_1 (or_1_out, comparator_1_eq, comparator_2_eq, comparator_3_eq);
  Comparator #(.width(4)) comparator_2 (.a(CODE), .b(4'b0111), .eq(comparator_2_eq));  // open: gt, lt
  Comparator #(.width(4)) comparator_3 (.a(CODE), .b(4'b0010), .eq(comparator_3_eq));  // open: gt, lt
  or or_2 (or_2_out, reset, or_1_out);
  assign controlled_buffer_2_out = or_1_out ? cdm_16_1_p4 : 16'bz;  // Controlled_Buffer controlled_buffer_2
  Pull_Resistor pull_resistor_3 (.node(controlled_buffer_2_out));
  assign controlled_buffer_3_out = or_1_out ? cdm_16_1_p2 : 16'bz;  // Controlled_Buffer controlled_buffer_3
  Pull_Resistor pull_resistor_4 (.node(controlled_buffer_3_out));
  assign controlled_buffer_4_out = or_1_out ? undriven : 16'bz;  // Controlled_Buffer controlled_buffer_4
  Pull_Resistor pull_resistor_5 (.node(controlled_buffer_4_out));
  Pull_Resistor pull_resistor_6 (.node(CLCK));
  Comparator #(.width(4)) comparator_4 (.a(4'b0001), .b(in_2), .eq(comparator_4_eq));  // open: gt, lt
  Comparator #(.width(4)) comparator_5 (.a(in_2), .b(4'b0010), .eq(comparator_5_eq));  // open: gt, lt
  // Probe on cdm_16_1_p2
  // Probe on undriven
  // CdM_16 cdm_16_1: pin names not known; wires that end beside it: or_1_out, cdm_16_1_p2, CLCK, cdm_16_1_p4, cdm_16_1_p5, cdm_16_1_p6, cdm_16_1_p7, {cdm_16_1_p8_2, cdm_16_1_p8}, cdm_16_1_p9, cdm_16_1_p10, cdm_16_1_p11, cdm_16_1_p12, mem, read, word, addr, cdm_16_1_p17, cdm_16_1_p18
  assign controlled_buffer_5_out = comparator_4_eq ? addr : 16'bz;  // Controlled_Buffer controlled_buffer_5
  assign controlled_buffer_6_out = comparator_5_eq ? addr : 16'bz;  // Controlled_Buffer controlled_buffer_6
  // Probe on cdm_16_1_p11
  // Probe on cdm_16_1_p10
  // Probe on cdm_16_1_p9
  // Probe on {cdm_16_1_p8_2, cdm_16_1_p8}
  // Probe on cdm_16_1_p7
  // Probe on cdm_16_1_p6
  // Probe on cdm_16_1_p5
  // Probe on cdm_16_1_p4
  // Probe on cdm_16_1_p12
  // Probe on addr
  assign data = not_1_out ? cdm_16_1_p17 : 16'bz;  // Controlled_Buffer controlled_buffer_7
  not not_1 (not_1_out, read);
  assign cdm_16_1_p18 = read ? data : 16'bz;  // Controlled_Buffer controlled_buffer_8
  // RAM ram_1: pin names not known; wires that end beside it: controlled_buffer_5_out, word, RAM, CLCK, read, data
  // RAM ram_2: pin names not known; wires that end beside it: controlled_buffer_6_out, word, RAM, CLCK, read, data
  and and_2 (and_2_out, addr[4], addr[5], addr[6], addr[7], addr[8], addr[9], addr[10], addr[11], addr[12], ~addr[13], addr[14], addr[15]);  // AND_Gate
  and and_3 (Isel, CLCK, and_2_out, read);
  not not_2 (not_2_out, Isel);
  and and_4 (RAM, not_2_out, mem);
  Divider #(.width(4)) divider_1 (.a(addr[3:0]), .b(4'b0010), .out(divider_1_out));  // open: upper, rem
  Multiplexer #(.select(4), .width(16)) multiplexer_1 (
    .in0(Y1), .in1(X1), .in2(Y2), .in3(X2), .out(data), .sel(divider_1_out), .en(Isel));  // open: in4, in5, in6, in7, in8, in9, in10, in11, in12, in13, in14, in15

  // Other names for the same wires on the sheet: bot_lvl[3:0] = in_2; Iaddr[3:0] = addr[3:0]
endmodule

module cdm_processing (
  input  in_1,
  input  [3:0] in_2,
  input  [7:0] from_digit,
  input  [7:0] from_letter,
  input  [7:0] to_digit,
  input  [7:0] to_letter,
  input  in_7,
  output [3:0] code,
  output out_9,
  output [1:0] counter,
  output code2_5,
  output [15:0] out_12,
  output [15:0] out_13,
  output [15:0] out_14,
  output lock,
  output out_16
);

  wire and_1_out, and_2_out, and_3_out, and_4_out, code2_7, code3, code4, code5, code6, code8,
       comparator_2_eq, comparator_3_eq, comparator_4_eq, comparator_5_eq, controlled_buffer_2_out,
       controlled_buffer_3_out, controlled_buffer_4_out, counter_1_q, counter_2_carry, counter_4_carry,
       or_1_out, or_2_out, or_3_out, or_4_out, pull_resistor_1_node, xor_1_out;
  wire [1:0] counter_2_q;
  wire [2:0] counter_4_q;
  wire [7:0] counter_3_q;
  wire [15:0] x1, x2, y1, y2;

  assign x1 = {{8{from_digit[7]}}, from_digit};  // Bit_Extender bit_extender_1
  assign y1 = {{8{from_letter[7]}}, from_letter};  // Bit_Extender bit_extender_2
  Pull_Resistor pull_resistor_1 (.node(pull_resistor_1_node));
  assign x2 = {{8{to_digit[7]}}, to_digit};  // Bit_Extender bit_extender_3
  assign y2 = {{8{to_letter[7]}}, to_letter};  // Bit_Extender bit_extender_4
  Counter #(.width(1), .max('h1)) counter_1 (
    .Q(counter_1_q), .clk(in_7), .clr(or_1_out));  // open: load, D, count, carry
  assign pull_resistor_1_node = code2_7 ? counter_2_carry : 1'bz;  // Controlled_Buffer controlled_buffer_1
  or or_1 (or_1_out, pull_resistor_1_node, code5);
  or or_2 (or_2_out, code2_7, and_1_out);
  and and_1 (and_1_out, code6, ~comparator_2_eq);  // AND_Gate
  xor xor_1 (xor_1_out, out_16, counter_4_carry);
  Pull_Resistor pull_resistor_2 (.node(out_16));
  and and_2 (and_2_out, counter_1_q, ~or_2_out);  // AND_Gate
  or or_3 (or_3_out, and_2_out, comparator_2_eq);
  Counter #(.width(2), .max('h2)) counter_2 (
    .Q(counter_2_q), .carry(counter_2_carry), .clk(xor_1_out));  // open: load, D, count, clr
  or or_4 (or_4_out, code4, code8, code3);
  Comparator #(.width(2), .mode("unsigned")) comparator_1 (.a(2'b00), .b(counter_2_q), .lt(out_9));  // open: gt, eq
  or or_5 (lock, code5, and_3_out);
  and and_3 (and_3_out, ~or_4_out, or_3_out);  // AND_Gate
  Counter counter_3 (
    .Q(counter_3_q), .clk(controlled_buffer_2_out), .clr(comparator_3_eq));  // open: load, D, count, carry
  assign controlled_buffer_2_out = out_16 ? in_1 : 1'bz;  // Controlled_Buffer controlled_buffer_2
  and and_4 (and_4_out, out_9, ~counter_4_carry);  // AND_Gate
  CDM cdm_1 (
    .CODE(code), .LINE3(out_12), .LINE2(out_13), .LINE1(out_14), .Y1(x1), .X1(y1), .Y2(x2), .X2(y2),
    .CLCK(controlled_buffer_3_out), .reset(comparator_3_eq), .in_2(in_2));
  assign controlled_buffer_3_out = lock ? in_1 : 1'bz;  // Controlled_Buffer controlled_buffer_3
  Counter #(.width(3), .max('h3)) counter_4 (
    .Q(counter_4_q), .carry(counter_4_carry), .clk(controlled_buffer_4_out), .clr(counter_4_carry));  // open: load, D, count
  assign controlled_buffer_4_out = and_4_out ? in_1 : 1'bz;  // Controlled_Buffer controlled_buffer_4
  Bit_Extender #(.in_width(3), .out_width(2), .\type ("sign")) bit_extender_5 (.in(counter_4_q), .out(counter));
  Comparator comparator_2 (.a(counter_3_q), .b(8'h6), .eq(comparator_2_eq));  // open: gt, lt
  Comparator comparator_3 (.a(counter_3_q), .b(8'h7), .eq(comparator_3_eq));  // open: gt, lt
  Comparator #(.width(4)) comparator_4 (.a(4'b0010), .b(code), .eq(comparator_4_eq));  // open: gt, lt
  Comparator #(.width(4)) comparator_5 (.a(4'b0111), .b(code), .eq(comparator_5_eq));  // open: gt, lt
  Comparator #(.width(4)) comparator_6 (.a(4'b0110), .b(code), .eq(code6));  // open: gt, lt
  Comparator #(.width(4)) comparator_7 (.a(4'b0101), .b(code), .eq(code5));  // open: gt, lt
  Comparator #(.width(4)) comparator_8 (.a(4'b0011), .b(code), .eq(code3));  // open: gt, lt
  Comparator #(.width(4)) comparator_9 (.a(4'b0100), .b(code), .eq(code4));  // open: gt, lt
  Comparator #(.width(4)) comparator_10 (.a(4'b1000), .b(code), .eq(code8));  // open: gt, lt
  or or_6 (code2_7, comparator_4_eq, comparator_5_eq);
  or or_7 (out_16, code2_7, code6);
  or or_8 (code2_5, code5, comparator_4_eq);

  // Other names for the same wires on the sheet: bot_lvl[3:0] = in_2; clock = in_1; ln1[15:0] = out_14;
  //   ln2[15:0] = out_13; ln3[15:0] = out_12
endmodule
module parsing_data (
  input  [15:0] in_1,
  output [7:0] out_2,
  output [31:0] out_3
);

  wire [3:0] bit_extender_3_out, bit_extender_4_out, bit_extender_5_out, bit_extender_6_out,
       transform_color_1_out_2, transform_color_2_out_2, transform_color_3_out_2, transform_color_4_out_2;
  wire [4:0] bit_extender_1_out, multiplier_1_out;

  assign bit_extender_1_out = {{4{1'b0}}, in_1[0]};  // Bit_Extender bit_extender_1
  assign out_2 = {{4{1'b0}}, in_1[3:0]};  // Bit_Extender bit_extender_2
  assign bit_extender_3_out = {{1{1'b0}}, in_1[15:13]};  // Bit_Extender bit_extender_3
  transform_color transform_color_1 (.in_1(bit_extender_3_out), .out_2(transform_color_1_out_2));
  assign bit_extender_4_out = {{1{1'b0}}, in_1[12:10]};  // Bit_Extender bit_extender_4
  transform_color transform_color_2 (.in_1(bit_extender_4_out), .out_2(transform_color_2_out_2));
  assign bit_extender_5_out = {{1{1'b0}}, in_1[9:7]};  // Bit_Extender bit_extender_5
  transform_color transform_color_3 (.in_1(bit_extender_5_out), .out_2(transform_color_3_out_2));
  assign bit_extender_6_out = {{1{1'b0}}, in_1[6:4]};  // Bit_Extender bit_extender_6
  transform_color transform_color_4 (.in_1(bit_extender_6_out), .out_2(transform_color_4_out_2));
  Multiplier #(.width(5)) multiplier_1 (
    .a(5'b00100), .b(bit_extender_1_out), .out(multiplier_1_out));  // open: cin, cout
  Shifter #(.width(32)) shifter_1 (
    .in({4'b0000, transform_color_4_out_2, 4'b0000, transform_color_3_out_2, 4'b0000, transform_color_2_out_2, 4'b0000, transform_color_1_out_2}),
    .\dist (multiplier_1_out), .out(out_3));
endmodule

module transform_color (
  input  [3:0] in_1,
  output [3:0] out_2
);

  wire comparator_1_eq, comparator_2_eq, comparator_3_eq, comparator_4_eq;
  wire [3:0] controlled_buffer_1_out, controlled_buffer_2_out, controlled_buffer_3_out,
       controlled_buffer_4_out;

  Comparator #(.width(4), .mode("unsigned")) comparator_1 (
    .a(4'b0001), .b(in_1), .eq(comparator_1_eq));  // open: gt, lt
  Comparator #(.width(4), .mode("unsigned")) comparator_2 (
    .a(4'b0010), .b(in_1), .eq(comparator_2_eq));  // open: gt, lt
  Comparator #(.width(4), .mode("unsigned")) comparator_3 (
    .a(in_1), .b(4'b0011), .eq(comparator_3_eq));  // open: gt, lt
  Comparator #(.width(4), .mode("unsigned")) comparator_4 (
    .a(in_1), .b(4'b0100), .eq(comparator_4_eq));  // open: gt, lt
  assign controlled_buffer_1_out = comparator_1_eq ? 4'b0010 : 4'bz;  // Controlled_Buffer controlled_buffer_1
  Pull_Resistor pull_resistor_1 (.node(controlled_buffer_1_out));
  assign controlled_buffer_2_out = comparator_2_eq ? 4'b0001 : 4'bz;  // Controlled_Buffer controlled_buffer_2
  Pull_Resistor pull_resistor_2 (.node(controlled_buffer_2_out));
  assign controlled_buffer_3_out = comparator_3_eq ? 4'b0100 : 4'bz;  // Controlled_Buffer controlled_buffer_3
  Pull_Resistor pull_resistor_3 (.node(controlled_buffer_3_out));
  assign controlled_buffer_4_out = comparator_4_eq ? 4'b0011 : 4'bz;  // Controlled_Buffer controlled_buffer_4
  Pull_Resistor pull_resistor_4 (.node(controlled_buffer_4_out));
  assign out_2 = controlled_buffer_1_out | controlled_buffer_2_out | controlled_buffer_3_out | controlled_buffer_4_out;  // OR_Gate or_1, 4 bits wide
endmodule

module displey (
  input  [3:0] in_1,
  input  in_2,
  output [31:0] _1,
  output [31:0] _2,
  output [31:0] _3,
  output [31:0] _4,
  output [31:0] _5,
  output [31:0] _6,
  output [31:0] _6_2
);

  wire and_1_out, and_2_out, and_3_out, and_4_out, comparator_1_eq, comparator_2_eq, comparator_3_eq,
       nor_1_out, not_1_out, not_2_out, not_3_out, not_4_out;

  assign _1 = in_2 ? 32'h7bdf00 : 32'bz;  // Controlled_Buffer controlled_buffer_1
  assign _2 = in_2 ? 32'h4a4400 : 32'bz;  // Controlled_Buffer controlled_buffer_2
  assign _3 = in_2 ? 32'h4a4400 : 32'bz;  // Controlled_Buffer controlled_buffer_3
  assign _4 = in_2 ? 32'h724400 : 32'bz;  // Controlled_Buffer controlled_buffer_4
  assign _5 = in_2 ? 32'h4a4400 : 32'bz;  // Controlled_Buffer controlled_buffer_5
  assign _6 = in_2 ? 32'h4a4400 : 32'bz;  // Controlled_Buffer controlled_buffer_6
  assign _6_2 = in_2 ? 32'h7bc400 : 32'bz;  // Controlled_Buffer controlled_buffer_7
  Comparator #(.width(4)) comparator_1 (.a(in_1), .b(4'b0011), .eq(comparator_1_eq));  // open: gt, lt
  and and_1 (and_1_out, comparator_1_eq, not_1_out);
  assign _1 = and_1_out ? 32'h55d200 : 32'bz;  // Controlled_Buffer controlled_buffer_8
  assign _2 = and_1_out ? 32'h549200 : 32'bz;  // Controlled_Buffer controlled_buffer_9
  assign _3 = and_1_out ? 32'h549a00 : 32'bz;  // Controlled_Buffer controlled_buffer_10
  assign _4 = and_1_out ? 32'h549600 : 32'bz;  // Controlled_Buffer controlled_buffer_11
  assign _5 = and_1_out ? 32'h549200 : 32'bz;  // Controlled_Buffer controlled_buffer_12
  assign _6 = and_1_out ? 32'h549200 : 32'bz;  // Controlled_Buffer controlled_buffer_13
  assign _6_2 = and_1_out ? 32'h29d200 : 32'bz;  // Controlled_Buffer controlled_buffer_14
  Comparator #(.width(4)) comparator_2 (.a(in_1), .b(4'b0100), .eq(comparator_2_eq));  // open: gt, lt
  and and_2 (and_2_out, comparator_2_eq, not_2_out);
  assign _1 = and_2_out ? 32'h21ef780 : 32'bz;  // Controlled_Buffer controlled_buffer_15
  assign _2 = and_2_out ? 32'h2128400 : 32'bz;  // Controlled_Buffer controlled_buffer_16
  assign _3 = and_2_out ? 32'h2128400 : 32'bz;  // Controlled_Buffer controlled_buffer_17
  assign _4 = and_2_out ? 32'h212f780 : 32'bz;  // Controlled_Buffer controlled_buffer_18
  assign _5 = and_2_out ? 32'h2121400 : 32'bz;  // Controlled_Buffer controlled_buffer_19
  assign _6 = and_2_out ? 32'h2121400 : 32'bz;  // Controlled_Buffer controlled_buffer_20
  assign _6_2 = and_2_out ? 32'h3def780 : 32'bz;  // Controlled_Buffer controlled_buffer_21
  Comparator #(.width(4)) comparator_3 (.a(in_1), .b(4'b1000), .eq(comparator_3_eq));  // open: gt, lt
  and and_3 (and_3_out, comparator_3_eq, not_3_out);
  assign _1 = and_3_out ? 32'h39c6540 : 32'bz;  // Controlled_Buffer controlled_buffer_22
  assign _2 = and_3_out ? 32'h2529540 : 32'bz;  // Controlled_Buffer controlled_buffer_23
  assign _3 = and_3_out ? 32'h2529540 : 32'bz;  // Controlled_Buffer controlled_buffer_24
  assign _4 = and_3_out ? 32'h25cf540 : 32'bz;  // Controlled_Buffer controlled_buffer_25
  assign _5 = and_3_out ? 32'h2529540 : 32'bz;  // Controlled_Buffer controlled_buffer_26
  assign _6 = and_3_out ? 32'h2529540 : 32'bz;  // Controlled_Buffer controlled_buffer_27
  assign _6_2 = and_3_out ? 32'h3929280 : 32'bz;  // Controlled_Buffer controlled_buffer_28
  and and_4 (and_4_out, nor_1_out, not_4_out);
  assign _1 = and_4_out ? 32'h7a1e8bde : 32'bz;  // Controlled_Buffer controlled_buffer_29
  assign _2 = and_4_out ? 32'h4a128a12 : 32'bz;  // Controlled_Buffer controlled_buffer_30
  assign _3 = and_4_out ? 32'h4a125212 : 32'bz;  // Controlled_Buffer controlled_buffer_31
  assign _4 = and_4_out ? 32'h7a1e23dc : 32'bz;  // Controlled_Buffer controlled_buffer_32
  assign _5 = and_4_out ? 32'h42122212 : 32'bz;  // Controlled_Buffer controlled_buffer_33
  assign _6 = and_4_out ? 32'h42122212 : 32'bz;  // Controlled_Buffer controlled_buffer_34
  assign _6_2 = and_4_out ? 32'h43d223d2 : 32'bz;  // Controlled_Buffer controlled_buffer_35
  not not_1 (not_1_out, in_2);
  not not_2 (not_2_out, in_2);
  not not_3 (not_3_out, in_2);
  nor nor_1 (nor_1_out, and_3_out, and_2_out, and_1_out);
  not not_4 (not_4_out, in_2);
  DotMatrix #(.inputtype("row"), .matrixcols(32)) dotmatrix_1 (
    .row0(32'h7bdf00), .row1(32'h4a4400), .row2(32'h4a4400), .row3(32'h724400), .row4(32'h4a4400),
    .row5(32'h4a4400), .row6(32'h7bc400));
  DotMatrix #(.inputtype("row"), .matrixcols(32)) dotmatrix_2 (
    .row0(32'h55d200), .row1(32'h549200), .row2(32'h549a00), .row3(32'h549600), .row4(32'h549200),
    .row5(32'h549200), .row6(32'h29d200));
  DotMatrix #(.inputtype("row"), .matrixcols(32)) dotmatrix_3 (
    .row0(32'h21ef780), .row1(32'h2128400), .row2(32'h2128400), .row3(32'h212f780), .row4(32'h2121400),
    .row5(32'h2121400), .row6(32'h3def780));
  DotMatrix #(.inputtype("row"), .matrixcols(32)) dotmatrix_4 (
    .row0(32'h39c6540), .row1(32'h2529540), .row2(32'h2529540), .row3(32'h25cf540), .row4(32'h2529540),
    .row5(32'h2529540), .row6(32'h3929280));
  DotMatrix #(.inputtype("row"), .matrixcols(32)) dotmatrix_5 (
    .row0(32'h7a1e8bde), .row1(32'h4a128a12), .row2(32'h4a125212), .row3(32'h7a1e23dc), .row4(32'h42122212),
    .row5(32'h42122212), .row6(32'h43d223d2));

  // Other names for the same wires on the sheet: code[3:0] = in_1
endmodule

module lvl_bot (
  input  in_1,
  input  in_2,
  output [3:0] out_3
);

  wire controlled_buffer_1_out, controlled_buffer_2_out, counter_1_carry, not_1_out, undriven;
  wire [3:0] counter_2_q;

  Counter #(.width(1), .max('h1)) counter_1 (
    .D(undriven), .count(undriven), .carry(counter_1_carry), .clk(controlled_buffer_1_out));  // open: load, Q, clr
  assign controlled_buffer_1_out = not_1_out ? in_1 : 1'bz;  // Controlled_Buffer controlled_buffer_1
  not not_1 (not_1_out, counter_1_carry);
  Counter #(.width(4), .max('h1)) counter_2 (
    .Q(counter_2_q), .clk(controlled_buffer_2_out));  // open: load, D, count, carry, clr
  assign controlled_buffer_2_out = not_1_out ? in_2 : 1'bz;  // Controlled_Buffer controlled_buffer_2
  Adder #(.width(4)) adder_1 (.a(4'b0001), .b(counter_2_q), .out(out_3));  // open: cin, cout
endmodule
